// Logisim project Lab_2_Circuit.circ as structural Verilog: 7 circuits, main circuit P2_7_Segment_Circuit
module P1_1_Logic_F (
  input  A,
  input  TTL_A,
  input  B,
  input  TTL_B,
  input  TTL_C,
  input  C,
  output TTL_OUTPUT,
  output OUTPUT_Gate
);

  wire ab_out, abc_out, ac_out, AND_2_Input_pin3, AND_2_Input_pin6, AND_2_Input_pin8, AND_2_Input_pin11,
       bc_out, n7408_1_pin6, OR_2_Input_pin4, OR_2_Input_pin5;

  and ab (ab_out, A, B);
  and abc (abc_out, A, B, C);
  and bc (bc_out, B, C);
  and ac (ac_out, A, C);
  or or_1 (OUTPUT_Gate, ab_out, abc_out, bc_out, ac_out);
  _7408 #(.ShowInternalStructure("true")) AND_2_Input (
    .pin1(TTL_C), .pin2(TTL_B), .pin3(AND_2_Input_pin3), .pin4(TTL_B), .pin5(TTL_A), .pin6(AND_2_Input_pin6),
    .pin13(TTL_C), .pin12(TTL_B), .pin11(AND_2_Input_pin11), .pin10(AND_2_Input_pin11), .pin9(TTL_A),
    .pin8(AND_2_Input_pin8));
  _7408 #(.ShowInternalStructure("true")) u_7408_1 (
    .pin4(TTL_A), .pin5(TTL_C), .pin6(n7408_1_pin6));  // open: pin1, pin2, pin3, pin13, pin12, pin11, pin10, pin9, pin8
  _7432 #(.ShowInternalStructure("true")) OR_2_Input (
    .pin4(OR_2_Input_pin4), .pin5(OR_2_Input_pin5), .pin6(TTL_OUTPUT), .pin13(n7408_1_pin6),
    .pin12(AND_2_Input_pin3), .pin11(OR_2_Input_pin4), .pin10(AND_2_Input_pin6), .pin9(AND_2_Input_pin8),
    .pin8(OR_2_Input_pin5));  // open: pin1, pin2, pin3

  // Notes on the sheet:
  //   F = abc + ab + bc + ca
  //   F = abc + ab + bc + ca
endmodule

module P1_1_Logic_G (
  input  A,
  input  B,
  input  TTL_A,
  input  C,
  input  TTL_B,
  input  TTL_C,
  output out_7,
  output OUTPUT_Gate
);

  wire AND_2_Input_pin8, AND_2_Input_pin11, N_AB_out, N_AC_B_out, N_BC_A_out, NOR_2_Input_pin1,
       NOR_2_Input_pin4, NOR_2_Input_pin10, not_1_out, not_2_out, not_3_out, OR_2_Input_pin11;

  not not_1 (not_1_out, A);
  not not_2 (not_2_out, B);
  not not_3 (not_3_out, C);
  and N_AB (N_AB_out, not_1_out, not_2_out);
  and N_AC_B (N_AC_B_out, B, not_3_out, not_1_out);
  and N_BC_A (N_BC_A_out, A, not_2_out, not_3_out);
  or or_1 (OUTPUT_Gate, N_AB_out, N_AC_B_out, N_BC_A_out);
  _7402 #(.ShowInternalStructure("true")) NOR_2_Input (
    .pin1(NOR_2_Input_pin1), .pin2(TTL_A), .pin3(TTL_B), .pin4(NOR_2_Input_pin4), .pin5(TTL_C), .pin6(TTL_A),
    .pin10(NOR_2_Input_pin10), .pin9(TTL_B), .pin8(TTL_C));  // open: pin13, pin12, pin11
  _7408 #(.ShowInternalStructure("true")) AND_2_Input (
    .pin13(TTL_B), .pin12(NOR_2_Input_pin4), .pin11(AND_2_Input_pin11), .pin10(NOR_2_Input_pin10),
    .pin9(TTL_A), .pin8(AND_2_Input_pin8));  // open: pin1, pin2, pin3, pin4, pin5, pin6
  _7432 #(.ShowInternalStructure("true")) OR_2_Input (
    .pin13(AND_2_Input_pin11), .pin12(AND_2_Input_pin8), .pin11(OR_2_Input_pin11), .pin10(OR_2_Input_pin11),
    .pin9(NOR_2_Input_pin1), .pin8(out_7));  // open: pin1, pin2, pin3, pin4, pin5, pin6

  // Notes on the sheet:
  //   G = a'b'+a'bc'+ab'c'
  //   G = a'b'+a'bc'+ab'c'
endmodule

module P2_7_Segment_Circuit (
  input  in_1,
  input  in_2,
  input  in_3,
  input  in_4,
  input  in_5,
  input  in_6,
  input  in_7,
  input  in_8,
  input  in_9,
  input  in_10
);

  wire or_1_out, p2_buttonpressed_1_a, p2_buttonpressed_1_b, p2_buttonpressed_1_c, p2_buttonpressed_1_d,
       p2_buttonpressed_1_e, p2_buttonpressed_1_f, p2_buttonpressed_1_g, p2_decoder_4x7_1_da,
       p2_decoder_4x7_1_db, p2_decoder_4x7_1_dc, p2_decoder_4x7_1_dd, p2_decoder_4x7_1_de,
       p2_decoder_4x7_1_df, p2_decoder_4x7_1_dg, p2_encoder_16x4_1_a, p2_encoder_16x4_1_b,
       p2_encoder_16x4_1_c, p2_encoder_16x4_1_d;

  P2_Encoder_16X4 p2_encoder_16x4_1 (
    .s0(in_1), .s1(in_2), .s2(in_3), .s3(in_4), .s4(in_5), .s5(in_6), .s6(in_7), .s7(in_8), .s8(in_9),
    .s9(in_10), .D(p2_encoder_16x4_1_d), .C(p2_encoder_16x4_1_c), .B(p2_encoder_16x4_1_b),
    .A(p2_encoder_16x4_1_a));
  or or_1 (or_1_out, in_1, in_2, in_3, in_4, in_5, in_6, in_7, in_8, in_9, in_10);
  P2_Decoder_4X7 p2_decoder_4x7_1 (
    .D(p2_encoder_16x4_1_d), .C(p2_encoder_16x4_1_c), .B(p2_encoder_16x4_1_b), .A(p2_encoder_16x4_1_a),
    .Da(p2_decoder_4x7_1_da), .Db(p2_decoder_4x7_1_db), .Dc(p2_decoder_4x7_1_dc), .Dd(p2_decoder_4x7_1_dd),
    .De(p2_decoder_4x7_1_de), .Df(p2_decoder_4x7_1_df), .Dg(p2_decoder_4x7_1_dg));
  P2_ButtonPressed p2_buttonpressed_1 (
    .Da(p2_decoder_4x7_1_da), .Db(p2_decoder_4x7_1_db), .Dc(p2_decoder_4x7_1_dc), .Dd(p2_decoder_4x7_1_dd),
    .De(p2_decoder_4x7_1_de), .Df(p2_decoder_4x7_1_df), .Dg(p2_decoder_4x7_1_dg), .Inp(or_1_out),
    .A(p2_buttonpressed_1_a), .B(p2_buttonpressed_1_b), .C(p2_buttonpressed_1_c), .D(p2_buttonpressed_1_d),
    .E(p2_buttonpressed_1_e), .F(p2_buttonpressed_1_f), .G(p2_buttonpressed_1_g));
  _7_Segment_Display u_7_segment_display_1 (
    .g(p2_buttonpressed_1_g), .f(p2_buttonpressed_1_f), .a(p2_buttonpressed_1_a), .b(p2_buttonpressed_1_b),
    .e(p2_buttonpressed_1_e), .d(p2_buttonpressed_1_d), .c(p2_buttonpressed_1_c));  // open: dp
endmodule

module P2_Encoder_16X4 (
  input  s0,
  input  s1,
  input  s2,
  input  s3,
  input  s4,
  input  s5,
  input  s6,
  input  s7,
  input  s8,
  input  s9,
  output D,
  output C,
  output B,
  output A
);

  wire n7432_1_pin2, n7432_1_pin5, n7432_1_pin11, n7432_2_pin4, n7432_2_pin11, n7432_3_pin5, n7432_3_pin11;

  _7432 #(.ShowInternalStructure("true")) u_7432_1 (
    .pin1(s3), .pin2(n7432_1_pin2), .pin3(D), .pin4(s1), .pin5(n7432_1_pin5), .pin6(n7432_1_pin2),
    .pin13(s9), .pin12(s7), .pin11(n7432_1_pin11), .pin10(n7432_1_pin11), .pin9(s5), .pin8(n7432_1_pin5));
  _7432 #(.ShowInternalStructure("true")) u_7432_2 (
    .pin4(n7432_2_pin4), .pin5(s2), .pin6(C), .pin13(s6), .pin12(s7), .pin11(n7432_2_pin11),
    .pin10(n7432_2_pin11), .pin9(s3), .pin8(n7432_2_pin4));  // open: pin1, pin2, pin3
  _7432 #(.ShowInternalStructure("true")) u_7432_3 (
    .pin4(s4), .pin5(n7432_3_pin5), .pin6(B), .pin13(s6), .pin12(s7), .pin11(n7432_3_pin11),
    .pin10(n7432_3_pin11), .pin9(s5), .pin8(n7432_3_pin5));  // open: pin1, pin2, pin3
  _7432 #(.ShowInternalStructure("true")) u_7432_4 (
    .pin10(s9), .pin9(s8), .pin8(A));  // open: pin1, pin2, pin3, pin4, pin5, pin6, pin13, pin12, pin11
endmodule

module P2_Decoder_4X7 (
  input  D,
  input  C,
  input  B,
  input  A,
  output Da,
  output Db,
  output Dc,
  output Dd,
  output De,
  output Df,
  output Dg
);

  wire n7402_1_pin1, n7402_1_pin3, n7402_1_pin9, n7402_1_pin10, n7402_1_pin11, n7402_1_pin13, n7408_1_pin8,
       n7408_1_pin11, n7408_2_pin8, n7408_2_pin11, n7408_3_pin6, n7408_3_pin8, n7408_3_pin11, n7408_4_pin8,
       n7408_4_pin11, n7408_5_pin3, n7408_5_pin8, n7408_5_pin11, n7408_6_pin3, n7408_6_pin8, n7408_6_pin11,
       n7411_1_pin8, n7432_1_pin11, n7432_3_pin5, n7432_3_pin11, n7432_4_pin11, n7432_5_pin2, n7432_5_pin3,
       n7432_5_pin11, n7432_6_pin5, n7432_6_pin11, n7432_7_pin5, n7432_7_pin11;

  _7402 #(.ShowInternalStructure("true")) u_7402_1 (
    .pin1(n7402_1_pin1), .pin2(B), .pin3(n7402_1_pin3), .pin13(n7402_1_pin13), .pin12(C),
    .pin11(n7402_1_pin11), .pin10(n7402_1_pin10), .pin9(n7402_1_pin9), .pin8(D));  // open: pin4, pin5, pin6
  _7408 #(.ShowInternalStructure("true")) u_7408_1 (
    .pin13(B), .pin12(D), .pin11(n7408_1_pin11), .pin10(n7402_1_pin1), .pin9(n7402_1_pin10),
    .pin8(n7408_1_pin8));  // open: pin1, pin2, pin3, pin4, pin5, pin6
  _7408 #(.ShowInternalStructure("true")) u_7408_2 (
    .pin13(C), .pin12(D), .pin11(n7408_2_pin11), .pin10(n7402_1_pin13), .pin9(n7402_1_pin10),
    .pin8(n7408_2_pin8));  // open: pin1, pin2, pin3, pin4, pin5, pin6
  _7432 #(.ShowInternalStructure("true")) u_7432_1 (
    .pin13(D), .pin12(n7402_1_pin13), .pin11(n7432_1_pin11), .pin10(n7432_1_pin11), .pin9(B), .pin8(Dc));  // open: pin1, pin2, pin3, pin4, pin5, pin6
  _7408 #(.ShowInternalStructure("true")) u_7408_3 (
    .pin4(C), .pin5(n7402_1_pin1), .pin6(n7408_3_pin6), .pin13(C), .pin12(n7402_1_pin10),
    .pin11(n7408_3_pin11), .pin10(n7402_1_pin1), .pin9(n7402_1_pin10), .pin8(n7408_3_pin8));  // open: pin1, pin2, pin3
  _7411 #(.ShowInternalStructure("true")) u_7411_1 (
    .pin11(D), .pin10(n7402_1_pin13), .pin9(B), .pin8(n7411_1_pin8));  // open: pin1, pin2, pin3, pin4, pin5, pin6, pin13, pin12
  _7408 #(.ShowInternalStructure("true")) u_7408_4 (
    .pin13(C), .pin12(n7402_1_pin10), .pin11(n7408_4_pin11), .pin10(n7402_1_pin1), .pin9(n7402_1_pin10),
    .pin8(n7408_4_pin8));  // open: pin1, pin2, pin3, pin4, pin5, pin6
  _7408 #(.ShowInternalStructure("true")) u_7408_5 (
    .pin1(B), .pin2(n7402_1_pin10), .pin3(n7408_5_pin3), .pin13(n7402_1_pin13), .pin12(B),
    .pin11(n7408_5_pin11), .pin10(n7402_1_pin13), .pin9(n7402_1_pin10), .pin8(n7408_5_pin8));  // open: pin4, pin5, pin6
  _7408 #(.ShowInternalStructure("true")) u_7408_6 (
    .pin1(C), .pin2(n7402_1_pin10), .pin3(n7408_6_pin3), .pin13(n7402_1_pin13), .pin12(B),
    .pin11(n7408_6_pin11), .pin10(C), .pin9(n7402_1_pin1), .pin8(n7408_6_pin8));  // open: pin4, pin5, pin6
  _7432 #(.ShowInternalStructure("true")) u_7432_2 (
    .pin10(n7408_4_pin11), .pin9(n7408_4_pin8), .pin8(De));  // open: pin1, pin2, pin3, pin4, pin5, pin6, pin13, pin12, pin11
  _7432 #(.ShowInternalStructure("true")) u_7432_3 (
    .pin4(n7408_1_pin8), .pin5(n7432_3_pin5), .pin6(Da), .pin13(A), .pin12(C), .pin11(n7432_3_pin11),
    .pin10(n7432_3_pin11), .pin9(n7408_1_pin11), .pin8(n7432_3_pin5));  // open: pin1, pin2, pin3
  _7432 #(.ShowInternalStructure("true")) u_7432_4 (
    .pin13(n7408_2_pin11), .pin12(n7408_2_pin8), .pin11(n7432_4_pin11), .pin10(n7432_4_pin11),
    .pin9(n7402_1_pin1), .pin8(Db));  // open: pin1, pin2, pin3, pin4, pin5, pin6
  _7432 #(.ShowInternalStructure("true")) u_7432_5 (
    .pin1(n7408_3_pin6), .pin2(n7432_5_pin2), .pin3(n7432_5_pin3), .pin4(n7432_5_pin3), .pin5(A), .pin6(Dd),
    .pin13(n7411_1_pin8), .pin12(n7408_3_pin8), .pin11(n7432_5_pin11), .pin10(n7432_5_pin11),
    .pin9(n7408_3_pin11), .pin8(n7432_5_pin2));
  _7432 #(.ShowInternalStructure("true")) u_7432_6 (
    .pin4(A), .pin5(n7432_6_pin5), .pin6(Df), .pin13(n7408_5_pin11), .pin12(n7408_5_pin3),
    .pin11(n7432_6_pin11), .pin10(n7432_6_pin11), .pin9(n7408_5_pin8), .pin8(n7432_6_pin5));  // open: pin1, pin2, pin3
  _7432 #(.ShowInternalStructure("true")) u_7432_7 (
    .pin4(n7408_6_pin8), .pin5(n7432_7_pin5), .pin6(Dg), .pin13(A), .pin12(n7408_6_pin11),
    .pin11(n7432_7_pin11), .pin10(n7432_7_pin11), .pin9(n7408_6_pin3), .pin8(n7432_7_pin5));  // open: pin1, pin2, pin3
  // also tied to GND on the sheet: {n7402_1_pin9, n7402_1_pin11, n7402_1_pin3}
endmodule

module P2_ButtonPressed (
  input  Da,
  input  Db,
  input  Dc,
  input  Dd,
  input  De,
  input  Df,
  input  Dg,
  input  Inp,
  output A,
  output B,
  output C,
  output D,
  output E,
  output F,
  output G
);

  and and_1 (A, Da, Inp);
  and and_2 (B, Db, Inp);
  and and_3 (C, Dc, Inp);
  and and_4 (D, Dd, Inp);
  and and_5 (E, De, Inp);
  and and_6 (F, Df, Inp);
  and and_7 (G, Dg, Inp);
endmodule

module P2_Old_Circuits (
  input  D,
  input  C,
  input  B,
  input  A,
  output Da,
  output Dc,
  output Db,
  output Dd,
  output De,
  output Df,
  output Dg
);

  wire B_NC_D_out, B_NC_out, B_ND_out, BD_out, C_ND2_out, C_ND_out, CD_out, NB_C_out, NB_ND2_out, NB_ND_out,
       NC_ND_out, not_1_out, not_2_out, not_3_out;

  not not_1 (not_1_out, D);
  not not_2 (not_2_out, C);
  not not_3 (not_3_out, B);
  and BD (BD_out, D, B);
  and NB_ND (NB_ND_out, not_1_out, not_3_out);
  and NC_ND (NC_ND_out, not_2_out, not_1_out);
  and CD (CD_out, C, D);
  and B_NC_D (B_NC_D_out, B, not_2_out, D);
  and C_ND (C_ND_out, C, not_1_out);
  and NB_C (NB_C_out, not_3_out, C);
  and NB_ND2 (NB_ND2_out, not_3_out, not_1_out);
  and C_ND2 (C_ND2_out, C, not_1_out);
  and B_NC (B_NC_out, B, not_2_out);
  and B_ND (B_ND_out, B, not_1_out);
  or or_1 (Da, BD_out, C, NB_ND_out, A);
  or or_2 (Dc, B, not_2_out, D);
  or or_3 (Db, NC_ND_out, not_3_out, CD_out);
  or or_4 (De, NB_ND2_out, C_ND2_out);
  or or_5 (Df, A, B_NC_out, NC_ND_out, B_ND_out);
  or or_6 (Dd, NB_ND_out, B_NC_D_out, A, C_ND_out, NB_C_out);
  or or_7 (Dg, B_NC_out, NB_C_out, C_ND_out, A);
endmodule
