// Logisim project Lab_3_Circuit.circ as structural Verilog: 6 circuits, main circuit P1_D_Flip_Flop
module P1_D_Flip_Flop (
  input  in_1,
  output out_2
);

  wire clock_1_out, nand_1_out, p1_d_latch_1_o;

  Clock clock_1 (.out(clock_1_out));
  nand nand_1 (nand_1_out, clock_1_out, clock_1_out);
  P1_D_Latch p1_d_latch_1 (.D(in_1), .CLK(nand_1_out), .O(p1_d_latch_1_o));
  P1_D_Latch p1_d_latch_2 (.D(p1_d_latch_1_o), .CLK(clock_1_out), .O(out_2));
endmodule

module P1_D_Latch (
  input  D,
  input  CLK,
  output O
);

  wire nand_1_out, nand_2_out, nand_3_out, nand_4_out, nand_5_out, nand_6_out, nand_7_out, nand_8_out,
       nand_9_out, nand_10_out, nand_11_out, nand_12_out;

  nand nand_1 (nand_1_out, D, D);
  nand nand_2 (nand_2_out, D, CLK);
  nand nand_3 (nand_3_out, CLK, nand_1_out);
  nand nand_4 (nand_4_out, nand_2_out, nand_2_out);
  nand nand_5 (nand_5_out, nand_3_out, nand_3_out);
  nand nand_6 (nand_6_out, nand_4_out, nand_4_out);
  nand nand_7 (nand_7_out, O, O);
  nand nand_8 (nand_8_out, nand_12_out, nand_12_out);
  nand nand_9 (nand_9_out, nand_5_out, nand_5_out);
  nand nand_10 (nand_10_out, nand_6_out, nand_7_out);
  nand nand_11 (nand_11_out, nand_8_out, nand_9_out);
  nand nand_12 (nand_12_out, nand_10_out, nand_10_out);
  nand nand_13 (O, nand_11_out, nand_11_out);
endmodule

module P2_Combinational_Logic (
  input  B,
  input  S_1,
  input  S_0,
  output LED,
  output N1,
  output N0
);

  wire and_1_out, and_2_out, and_3_out, and_4_out, and_5_out, and_6_out, and_7_out, and_8_out, and_9_out,
       and_10_out, and_11_out, not_1_out, not_2_out, TTL_7400_out, TTL_7408_out;

  not TTL_7400 (TTL_7400_out, B);
  not not_1 (not_1_out, S_1);
  not not_2 (not_2_out, S_0);
  and TTL_7408 (TTL_7408_out, TTL_7400_out, not_1_out, S_0);
  and and_1 (and_1_out, not_1_out, S_0, B);
  and and_2 (and_2_out, S_1, not_2_out, TTL_7400_out);
  and and_3 (and_3_out, S_1, not_2_out, B);
  and and_4 (and_4_out, not_1_out, S_0, TTL_7400_out);
  and and_5 (and_5_out, S_1, not_2_out, TTL_7400_out);
  and and_6 (and_6_out, S_1, not_2_out, B);
  and and_7 (and_7_out, S_1, S_0, B);
  and and_8 (and_8_out, not_1_out, not_2_out, B);
  and and_9 (and_9_out, not_1_out, S_0, B);
  and and_10 (and_10_out, S_1, not_2_out, B);
  and and_11 (and_11_out, S_1, S_0, B);
  or TTL_7432 (LED, TTL_7408_out, and_1_out, and_2_out, and_3_out);
  or or_1 (N1, and_4_out, and_5_out, and_6_out, and_7_out);
  or or_2 (N0, and_8_out, and_9_out, and_10_out, and_11_out);
endmodule

module P2_Controller (
);

  wire button_1_out, clock_1_out, d_ff_1_q, d_ff_2_q, p2_combinational_logic_1_led,
       p2_combinational_logic_1_n0, p2_combinational_logic_1_n1;

  Clock clock_1 (.out(clock_1_out));
  Button button_1 (.out(button_1_out));
  D_Flip_Flop d_ff_1 (.D(p2_combinational_logic_1_n1), .clk(clock_1_out), .Q(d_ff_1_q));  // open: Qn, preset, reset
  D_Flip_Flop d_ff_2 (.D(p2_combinational_logic_1_n0), .clk(clock_1_out), .Q(d_ff_2_q));  // open: Qn, preset, reset
  LED led_1 (.in(p2_combinational_logic_1_led));
  P2_Combinational_Logic p2_combinational_logic_1 (
    .B(button_1_out), .S_1(d_ff_1_q), .S_0(d_ff_2_q), .LED(p2_combinational_logic_1_led),
    .N1(p2_combinational_logic_1_n1), .N0(p2_combinational_logic_1_n0));
endmodule

module P3_Combinational_Logic (
  input  B3,
  input  B2,
  input  B1,
  input  B0,
  input  INP
);

  wire and_1_out, and_2_out, and_3_out, and_4_out, and_5_out, and_6_out, and_7_out, and_8_out, clock_1_out,
       clock_2_out, clock_3_out, clock_4_out, clock_5_out, clock_6_out, clock_7_out, clock_8_out, d_ff_1_q,
       d_ff_2_q, d_ff_3_q, d_ff_4_q, d_ff_5_q, d_ff_6_q, d_ff_7_q, d_ff_8_q, multiplexer_1_out,
       multiplexer_2_out, multiplexer_3_out, multiplexer_4_out, multiplexer_5_out, multiplexer_6_out,
       multiplexer_7_out, multiplexer_8_out, not_1_out, not_2_out, not_3_out;

  not not_1 (not_1_out, B2);
  not not_2 (not_2_out, B1);
  not not_3 (not_3_out, B0);
  Clock clock_1 (.out(clock_1_out));
  and and_1 (and_1_out, not_1_out, not_2_out, not_3_out, INP);
  Multiplexer multiplexer_1 (.in0(d_ff_1_q), .in1(B3), .out(multiplexer_1_out), .sel(and_1_out));
  D_Flip_Flop d_ff_1 (.D(multiplexer_1_out), .clk(clock_1_out), .Q(d_ff_1_q));  // open: Qn, preset, reset
  LED Headlight (.in(d_ff_1_q));
  Clock clock_2 (.out(clock_2_out));
  and and_2 (and_2_out, not_1_out, B1, not_3_out, INP);
  Clock clock_3 (.out(clock_3_out));
  and and_3 (and_3_out, not_1_out, not_2_out, B0, INP);
  Multiplexer multiplexer_2 (.in0(d_ff_2_q), .in1(B3), .out(multiplexer_2_out), .sel(and_3_out));
  D_Flip_Flop d_ff_2 (.D(multiplexer_2_out), .clk(clock_2_out), .Q(d_ff_2_q));  // open: Qn, preset, reset
  Multiplexer multiplexer_3 (.in0(d_ff_3_q), .in1(B3), .out(multiplexer_3_out), .sel(and_2_out));
  D_Flip_Flop d_ff_3 (.D(multiplexer_3_out), .clk(clock_3_out), .Q(d_ff_3_q));  // open: Qn, preset, reset
  LED D1 (.in(d_ff_2_q));
  LED D2 (.in(d_ff_3_q));
  and and_4 (and_4_out, not_1_out, B1, B0, INP);
  Clock clock_4 (.out(clock_4_out));
  and and_5 (and_5_out, B2, not_2_out, not_3_out, INP);
  D_Flip_Flop d_ff_4 (.D(multiplexer_5_out), .clk(clock_5_out), .Q(d_ff_4_q));  // open: Qn, preset, reset
  Clock clock_5 (.out(clock_5_out));
  Multiplexer multiplexer_4 (.in0(d_ff_5_q), .in1(B3), .out(multiplexer_4_out), .sel(and_4_out));
  D_Flip_Flop d_ff_5 (.D(multiplexer_4_out), .clk(clock_4_out), .Q(d_ff_5_q));  // open: Qn, preset, reset
  Multiplexer multiplexer_5 (.in0(d_ff_4_q), .in1(B3), .out(multiplexer_5_out), .sel(and_5_out));
  LED D4 (.in(d_ff_4_q));
  LED D3 (.in(d_ff_5_q));
  Clock clock_6 (.out(clock_6_out));
  and and_6 (and_6_out, B2, B1, not_3_out, INP);
  Clock clock_7 (.out(clock_7_out));
  and and_7 (and_7_out, B2, not_2_out, B0, INP);
  Multiplexer multiplexer_6 (.in0(d_ff_6_q), .in1(B3), .out(multiplexer_6_out), .sel(and_7_out));
  D_Flip_Flop d_ff_6 (.D(multiplexer_6_out), .clk(clock_6_out), .Q(d_ff_6_q));  // open: Qn, preset, reset
  Multiplexer multiplexer_7 (.in0(d_ff_7_q), .in1(B3), .out(multiplexer_7_out), .sel(and_6_out));
  D_Flip_Flop d_ff_7 (.D(multiplexer_7_out), .clk(clock_7_out), .Q(d_ff_7_q));  // open: Qn, preset, reset
  LED L_Light (.in(d_ff_6_q));
  LED R_Light (.in(d_ff_7_q));
  and and_8 (and_8_out, B2, B1, B0, INP);
  Clock clock_8 (.out(clock_8_out));
  Multiplexer multiplexer_8 (.in0(d_ff_8_q), .in1(B3), .out(multiplexer_8_out), .sel(and_8_out));
  D_Flip_Flop d_ff_8 (.D(multiplexer_8_out), .clk(clock_8_out), .Q(d_ff_8_q));  // open: Qn, preset, reset
  LED Windows_Wiper (.in(d_ff_8_q));
endmodule

module P3_Timing_Diagram (
);


  // Notes on the sheet:
  //   CLK
  //   B3
  //   B2
  //   B1
  //   B0
  //   Headlights
  //   D1
  //   D2
  //   D3
  //   D4
  //   Left Indecator
  //   Right Indecator
  //   Windshield Wipers
endmodule
