// Logisim project L4_Final_Submission.circ as structural Verilog: 25 circuits, main circuit main
module main (
  input  [7:0] in_1,
  input  [7:0] in_2,
  input  Enable,
  input  [7:0] in_4,
  input  [7:0] in_5,
  input  [7:0] in_6,
  input  [7:0] in_7,
  output [7:0] out_8,
  output [7:0] out_9,
  output [7:0] out_10,
  output [7:0] out_11,
  output [7:0] out_12
);

  wire clock_1_out;
  wire [7:0] fakecpu_evan_1_addressout, fakecpu_evan_1_controlout, fakecpu_evan_1_databusout,
       inputmodule_po_1_databus_out, memory_ot_1_databus_out, portio_1_p2;

  Clock clock_1 (.out(clock_1_out));
  InputModule_PO inputmodule_po_1 (
    .Control_In(fakecpu_evan_1_controlout), .Address_In(fakecpu_evan_1_addressout), .Input_1(in_4),
    .Input_2(in_5), .Input_3(in_6), .Input_4(in_7), .Clk(clock_1_out), .Enable(Enable),
    .Databus_out(inputmodule_po_1_databus_out));  // open: Databus_control
  // PortIO portio_1: pin names not known; wires that end beside it: inputmodule_po_1_databus_out, portio_1_p2
  FakeCpu_Evan fakecpu_evan_1 (
    .logicSignal(in_1), .AddressSignal(in_2), .DataBusIn(portio_1_p2), .Clk(clock_1_out), .Enable(Enable),
    .ControlOut(fakecpu_evan_1_controlout), .AddressOut(fakecpu_evan_1_addressout),
    .DataBusOut(fakecpu_evan_1_databusout), .Buffer_Value(out_8));  // open: DatabusWrite
  // PortIO portio_2: pin names not known; wires that end beside it: fakecpu_evan_1_databusout, portio_1_p2
  Memory_OT memory_ot_1 (
    .Control_In(fakecpu_evan_1_controlout), .Address_In(fakecpu_evan_1_addressout), .Databus_In(portio_1_p2),
    .Enable(Enable), .Clk(clock_1_out), .Databus_out(memory_ot_1_databus_out));  // open: Databus_control
  // PortIO portio_3: pin names not known; wires that end beside it: memory_ot_1_databus_out, portio_1_p2
  OutputModule_PO outputmodule_po_1 (
    .Enable(Enable), .Control_In(fakecpu_evan_1_controlout), .Address_In(fakecpu_evan_1_addressout),
    .Databus_In(portio_1_p2), .Clk(clock_1_out), .Output_1(out_9), .Output_2(out_10), .Output_3(out_11),
    .Output_4(out_12));

  // Notes on the sheet:
  //   clock
  //   data
  //   address
  //   control
endmodule

module FakeCpu_Evan (
  input  [7:0] logicSignal,
  input  [7:0] AddressSignal,
  input  [7:0] DataBusIn,
  input  Clk,
  input  Enable,
  output [7:0] ControlOut,
  output [7:0] AddressOut,
  output [7:0] DataBusOut,
  output DatabusWrite,
  output [7:0] Buffer_Value
);

  wire comparator_1_eq, comparator_2_eq, or_1_out;

  Register #(.trigger("high")) buffers (.D(DataBusIn), .en(Enable), .clk(Clk), .Q(Buffer_Value));  // open: clr
  Comparator comparator_1 (.a(8'h5), .b(logicSignal), .eq(comparator_1_eq));  // open: gt, lt
  Comparator comparator_2 (.a(8'h3), .b(logicSignal), .eq(comparator_2_eq));  // open: gt, lt
  or or_1 (or_1_out, comparator_1_eq, comparator_2_eq);
  and and_1 (DatabusWrite, or_1_out, Enable);

  assign AddressOut = AddressSignal;
  assign ControlOut = logicSignal;
  assign DataBusOut = Buffer_Value;

  // Notes on the sheet:
  //   And write it to data bus out
  //   Buffer will take in data from dataBusIn
endmodule

module Bonus (
  input  Left,
  input  Right,
  input  Left1,
  input  Right1
);

  wire clock_1_out, clock_2_out, decoder_1_out1, decoder_1_out2, decoder_1_out3, decoder_1_out4,
       decoder_1_out5, decoder_1_out6, decoder_1_out7, decoder_1_out8, decoder_1_out9, decoder_1_out10,
       decoder_1_out11, decoder_1_out12, decoder_1_out13, decoder_1_out14, decoder_1_out15, decoder_1_out16,
       decoder_1_out17, decoder_1_out18, decoder_1_out19, decoder_1_out20, decoder_1_out21, decoder_1_out22,
       decoder_1_out23, decoder_1_out24, decoder_1_out25, decoder_2_out1, decoder_2_out2, decoder_2_out3,
       decoder_2_out4, decoder_2_out5, decoder_2_out6, decoder_2_out7, decoder_2_out8, decoder_2_out9,
       decoder_2_out10, decoder_2_out11, decoder_2_out12, decoder_2_out13, decoder_2_out14, decoder_2_out15,
       decoder_2_out16, decoder_2_out17, decoder_2_out18, decoder_2_out19, decoder_2_out20, decoder_2_out21,
       decoder_2_out22, decoder_2_out23, decoder_2_out24, decoder_2_out25, xnor_1_out, xnor_2_out;
  wire [4:0] counter_1_q, rom_1_data;
  wire [7:0] counter_2_q;
  wire [7:5] counter_1_q_2;

  Clock clock_1 (.out(clock_1_out));
  Clock clock_2 (.out(clock_2_out));
  xnor xnor_1 (xnor_1_out, Left, Right);
  Counter #(.max('h19)) counter_1 (
    .clr(xnor_1_out), .up(Right), .clk(clock_1_out), .Q({counter_1_q_2, counter_1_q}));  // open: load, count, D, carry
  xnor xnor_2 (xnor_2_out, Left1, Right1);
  Counter #(.max('h19)) counter_2 (
    .clr(xnor_2_out), .up(Right1), .clk(clock_2_out), .Q(counter_2_q));  // open: load, count, D, carry
  ROM #(.dataWidth(5)) rom_1 (.addr(counter_2_q), .data(rom_1_data));
  Decoder #(.select(5)) decoder_1 (
    .out1(decoder_1_out1), .out2(decoder_1_out2), .out3(decoder_1_out3), .out4(decoder_1_out4),
    .out5(decoder_1_out5), .out6(decoder_1_out6), .out7(decoder_1_out7), .out8(decoder_1_out8),
    .out9(decoder_1_out9), .out10(decoder_1_out10), .out11(decoder_1_out11), .out12(decoder_1_out12),
    .out13(decoder_1_out13), .out14(decoder_1_out14), .out15(decoder_1_out15), .out16(decoder_1_out16),
    .out17(decoder_1_out17), .out18(decoder_1_out18), .out19(decoder_1_out19), .out20(decoder_1_out20),
    .out21(decoder_1_out21), .out22(decoder_1_out22), .out23(decoder_1_out23), .out24(decoder_1_out24),
    .out25(decoder_1_out25), .sel(counter_1_q));  // open: out0, out26, out27, out28, out29, out30, out31, en
  LedBar #(.matrixcols(25)) ledbar_1 (
    .led0(decoder_1_out1), .led1(decoder_1_out2), .led2(decoder_1_out3), .led3(decoder_1_out4),
    .led4(decoder_1_out5), .led5(decoder_1_out6), .led6(decoder_1_out7), .led7(decoder_1_out8),
    .led8(decoder_1_out9), .led9(decoder_1_out10), .led10(decoder_1_out11), .led11(decoder_1_out12),
    .led12(decoder_1_out13), .led13(decoder_1_out14), .led14(decoder_1_out15), .led15(decoder_1_out16),
    .led16(decoder_1_out17), .led17(decoder_1_out18), .led18(decoder_1_out19), .led19(decoder_1_out20),
    .led20(decoder_1_out21), .led21(decoder_1_out22), .led22(decoder_1_out23), .led23(decoder_1_out24),
    .led24(decoder_1_out25));
  Decoder #(.select(5)) decoder_2 (
    .out1(decoder_2_out1), .out2(decoder_2_out2), .out3(decoder_2_out3), .out4(decoder_2_out4),
    .out5(decoder_2_out5), .out6(decoder_2_out6), .out7(decoder_2_out7), .out8(decoder_2_out8),
    .out9(decoder_2_out9), .out10(decoder_2_out10), .out11(decoder_2_out11), .out12(decoder_2_out12),
    .out13(decoder_2_out13), .out14(decoder_2_out14), .out15(decoder_2_out15), .out16(decoder_2_out16),
    .out17(decoder_2_out17), .out18(decoder_2_out18), .out19(decoder_2_out19), .out20(decoder_2_out20),
    .out21(decoder_2_out21), .out22(decoder_2_out22), .out23(decoder_2_out23), .out24(decoder_2_out24),
    .out25(decoder_2_out25), .sel(rom_1_data));  // open: out0, out26, out27, out28, out29, out30, out31, en
  LedBar #(.matrixcols(25)) ledbar_2 (
    .led0(decoder_2_out1), .led1(decoder_2_out2), .led2(decoder_2_out3), .led3(decoder_2_out4),
    .led4(decoder_2_out5), .led5(decoder_2_out6), .led6(decoder_2_out7), .led7(decoder_2_out8),
    .led8(decoder_2_out9), .led9(decoder_2_out10), .led10(decoder_2_out11), .led11(decoder_2_out12),
    .led12(decoder_2_out13), .led13(decoder_2_out14), .led14(decoder_2_out15), .led15(decoder_2_out16),
    .led16(decoder_2_out17), .led17(decoder_2_out18), .led18(decoder_2_out19), .led19(decoder_2_out20),
    .led20(decoder_2_out21), .led21(decoder_2_out22), .led22(decoder_2_out23), .led23(decoder_2_out24),
    .led24(decoder_2_out25));

  // Notes on the sheet:
  //   contents of rom_1 (hex, n*v repeats v):
  //   0 1 2 3 4 5 6 7 8 9 a b c d e f 10 11 12 13 14 15 16 17 18 19 1a 1b 1c 1d 1e 1f
endmodule

module OutputModule_PO (
  input  Enable,
  input  [7:0] Control_In,
  input  [7:0] Address_In,
  input  [7:0] Databus_In,
  input  Clk,
  output [7:0] Output_1,
  output [7:0] Output_2,
  output [7:0] Output_3,
  output [7:0] Output_4
);

  wire and_1_out, and_2_out, comparator_1_eq, demultiplexer_1_out0, demultiplexer_1_out1,
       demultiplexer_1_out2, demultiplexer_1_out3, nor_1_out;
  wire [7:0] p2_subtractor_po_1_s;

  Comparator comparator_1 (.a(8'h5), .b(Control_In), .eq(comparator_1_eq));  // open: gt, lt
  and and_1 (and_1_out, Enable, comparator_1_eq);
  P2_Subtractor_PO p2_subtractor_po_1 (.A(Address_In), .B(8'h5), .S(p2_subtractor_po_1_s));
  nor nor_1 (nor_1_out, p2_subtractor_po_1_s[7], p2_subtractor_po_1_s[6], p2_subtractor_po_1_s[5], p2_subtractor_po_1_s[4], p2_subtractor_po_1_s[3], p2_subtractor_po_1_s[2]);
  and and_2 (and_2_out, and_1_out, nor_1_out);
  Demultiplexer #(.select(2)) demultiplexer_1 (
    .out0(demultiplexer_1_out0), .out1(demultiplexer_1_out1), .out2(demultiplexer_1_out2),
    .out3(demultiplexer_1_out3), .in(and_2_out), .sel(p2_subtractor_po_1_s[1:0]));
  Register register_1 (.D(Databus_In), .en(demultiplexer_1_out0), .clk(Clk), .Q(Output_1));  // open: clr
  Register register_2 (.D(Databus_In), .en(demultiplexer_1_out1), .clk(Clk), .Q(Output_2));  // open: clr
  Register register_3 (.D(Databus_In), .en(demultiplexer_1_out2), .clk(Clk), .Q(Output_3));  // open: clr
  Register register_4 (.D(Databus_In), .en(demultiplexer_1_out3), .clk(Clk), .Q(Output_4));  // open: clr
endmodule

module InputModule_PO (
  input  [7:0] Control_In,
  input  [7:0] Address_In,
  input  [7:0] Input_1,
  input  [7:0] Input_2,
  input  [7:0] Input_3,
  input  [7:0] Input_4,
  input  Clk,
  input  Enable,
  output [7:0] Databus_out,
  output Databus_control
);

  wire and_1_out, comparator_1_eq, nor_1_out;
  wire [7:0] p2_subtractor_po_1_s, register_1_q, register_2_q, register_3_q, register_4_q;

  Comparator comparator_1 (.a(8'h4), .b(Control_In), .eq(comparator_1_eq));  // open: gt, lt
  P2_Subtractor_PO p2_subtractor_po_1 (.A(Address_In), .B(8'h1), .S(p2_subtractor_po_1_s));
  nor nor_1 (nor_1_out, p2_subtractor_po_1_s[7], p2_subtractor_po_1_s[6], p2_subtractor_po_1_s[5], p2_subtractor_po_1_s[4], p2_subtractor_po_1_s[3], p2_subtractor_po_1_s[2]);
  and and_1 (and_1_out, nor_1_out, Enable);
  Register register_1 (.D(Input_1), .clk(Clk), .Q(register_1_q));  // open: en, clr
  Register register_2 (.D(Input_2), .clk(Clk), .Q(register_2_q));  // open: en, clr
  Register register_3 (.D(Input_3), .clk(Clk), .Q(register_3_q));  // open: en, clr
  Register register_4 (.D(Input_4), .clk(Clk), .Q(register_4_q));  // open: en, clr
  Multiplexer #(.select(2), .width(8)) multiplexer_1 (
    .in0(register_1_q), .in1(register_2_q), .in2(register_3_q), .in3(register_4_q), .out(Databus_out),
    .sel(p2_subtractor_po_1_s[1:0]));
  and and_2 (Databus_control, comparator_1_eq, and_1_out);

  // Notes on the sheet:
  //   change address system
endmodule

module P2_8_bit_Adder_PO (
  input  Ci,
  input  [7:0] A,
  input  [7:0] B,
  output Co,
  output [7:0] S
);

  wire p2_1_bit_adder_po_1_co, p2_1_bit_adder_po_2_co, p2_1_bit_adder_po_3_co, p2_1_bit_adder_po_4_co,
       p2_1_bit_adder_po_5_co, p2_1_bit_adder_po_6_co, p2_1_bit_adder_po_7_co;

  P2_1_bit_Adder_PO p2_1_bit_adder_po_1 (.A(A[0]), .B(B[0]), .Ci(Ci), .Co(p2_1_bit_adder_po_1_co), .S(S[0]));
  P2_1_bit_Adder_PO p2_1_bit_adder_po_2 (
    .A(A[1]), .B(B[1]), .Ci(p2_1_bit_adder_po_1_co), .Co(p2_1_bit_adder_po_2_co), .S(S[1]));
  P2_1_bit_Adder_PO p2_1_bit_adder_po_3 (
    .A(A[2]), .B(B[2]), .Ci(p2_1_bit_adder_po_2_co), .Co(p2_1_bit_adder_po_3_co), .S(S[2]));
  P2_1_bit_Adder_PO p2_1_bit_adder_po_4 (
    .A(A[3]), .B(B[3]), .Ci(p2_1_bit_adder_po_3_co), .Co(p2_1_bit_adder_po_4_co), .S(S[3]));
  P2_1_bit_Adder_PO p2_1_bit_adder_po_5 (
    .A(A[4]), .B(B[4]), .Ci(p2_1_bit_adder_po_4_co), .Co(p2_1_bit_adder_po_5_co), .S(S[4]));
  P2_1_bit_Adder_PO p2_1_bit_adder_po_6 (
    .A(A[5]), .B(B[5]), .Ci(p2_1_bit_adder_po_5_co), .Co(p2_1_bit_adder_po_6_co), .S(S[5]));
  P2_1_bit_Adder_PO p2_1_bit_adder_po_7 (
    .A(A[6]), .B(B[6]), .Ci(p2_1_bit_adder_po_6_co), .Co(p2_1_bit_adder_po_7_co), .S(S[6]));
  P2_1_bit_Adder_PO p2_1_bit_adder_po_8 (.A(A[7]), .B(B[7]), .Ci(p2_1_bit_adder_po_7_co), .Co(Co), .S(S[7]));
endmodule

module P2_L_Shifter_PO (
  input  [7:0] in_1,
  input  in_2,
  input  in_3,
  input  in_4,
  output [7:0] out_5
);

  wire [7:0] p2_l_shifter_2_times_po_1_data_out, p2_l_shifter_4_times_po_1_data_out;

  P2_L_Shifter_4_times_PO p2_l_shifter_4_times_po_1 (
    .Data_in(in_1), .X(in_2), .Data_out(p2_l_shifter_4_times_po_1_data_out));
  P2_L_Shifter_2_times_PO p2_l_shifter_2_times_po_1 (
    .Data_in(p2_l_shifter_4_times_po_1_data_out), .Y(in_3), .Data_out(p2_l_shifter_2_times_po_1_data_out));
  P2_L_Shifter_1_times_PO p2_l_shifter_1_times_po_1 (
    .Data_in(p2_l_shifter_2_times_po_1_data_out), .Z(in_4), .Data_out(out_5));
endmodule

module P2_Subtractor_PO (
  input  [7:0] A,
  input  [7:0] B,
  output [7:0] S
);

  wire [7:0] not_1_out;

  assign not_1_out = ~B;  // NOT_Gate not_1, 8 bits wide
  P2_8_bit_Adder_PO p2_8_bit_adder_po_1 (.Ci(1'b1), .A(A), .B(not_1_out), .S(S));  // open: Co
endmodule

module P2_8_bit_Magnitude_Comparitor_PO (
  input  [7:0] A,
  input  [7:0] B,
  output Greater,
  output Equal,
  output Less
);

  wire p2_magnitude_comparitor_po_1_oeq, p2_magnitude_comparitor_po_1_ogt, p2_magnitude_comparitor_po_1_olt,
       p2_magnitude_comparitor_po_2_oeq, p2_magnitude_comparitor_po_2_ogt, p2_magnitude_comparitor_po_2_olt,
       p2_magnitude_comparitor_po_3_oeq, p2_magnitude_comparitor_po_3_ogt, p2_magnitude_comparitor_po_3_olt,
       p2_magnitude_comparitor_po_4_oeq, p2_magnitude_comparitor_po_4_ogt, p2_magnitude_comparitor_po_4_olt,
       p2_magnitude_comparitor_po_5_oeq, p2_magnitude_comparitor_po_5_ogt, p2_magnitude_comparitor_po_5_olt,
       p2_magnitude_comparitor_po_6_oeq, p2_magnitude_comparitor_po_6_ogt, p2_magnitude_comparitor_po_6_olt,
       p2_magnitude_comparitor_po_7_oeq, p2_magnitude_comparitor_po_7_ogt, p2_magnitude_comparitor_po_7_olt;

  P2_Magnitude_Comparitor_PO p2_magnitude_comparitor_po_1 (
    .A(A[7]), .B(B[7]), .lgt(1'b0), .leq(1'b1), .llt(1'b0), .ogt(p2_magnitude_comparitor_po_1_ogt),
    .oeq(p2_magnitude_comparitor_po_1_oeq), .olt(p2_magnitude_comparitor_po_1_olt));
  P2_Magnitude_Comparitor_PO p2_magnitude_comparitor_po_2 (
    .A(A[6]), .B(B[6]), .lgt(p2_magnitude_comparitor_po_1_ogt), .leq(p2_magnitude_comparitor_po_1_oeq),
    .llt(p2_magnitude_comparitor_po_1_olt), .ogt(p2_magnitude_comparitor_po_2_ogt),
    .oeq(p2_magnitude_comparitor_po_2_oeq), .olt(p2_magnitude_comparitor_po_2_olt));
  P2_Magnitude_Comparitor_PO p2_magnitude_comparitor_po_3 (
    .A(A[5]), .B(B[5]), .lgt(p2_magnitude_comparitor_po_2_ogt), .leq(p2_magnitude_comparitor_po_2_oeq),
    .llt(p2_magnitude_comparitor_po_2_olt), .ogt(p2_magnitude_comparitor_po_3_ogt),
    .oeq(p2_magnitude_comparitor_po_3_oeq), .olt(p2_magnitude_comparitor_po_3_olt));
  P2_Magnitude_Comparitor_PO p2_magnitude_comparitor_po_4 (
    .A(A[4]), .B(B[4]), .lgt(p2_magnitude_comparitor_po_3_ogt), .leq(p2_magnitude_comparitor_po_3_oeq),
    .llt(p2_magnitude_comparitor_po_3_olt), .ogt(p2_magnitude_comparitor_po_4_ogt),
    .oeq(p2_magnitude_comparitor_po_4_oeq), .olt(p2_magnitude_comparitor_po_4_olt));
  P2_Magnitude_Comparitor_PO p2_magnitude_comparitor_po_5 (
    .A(A[3]), .B(B[3]), .lgt(p2_magnitude_comparitor_po_4_ogt), .leq(p2_magnitude_comparitor_po_4_oeq),
    .llt(p2_magnitude_comparitor_po_4_olt), .ogt(p2_magnitude_comparitor_po_5_ogt),
    .oeq(p2_magnitude_comparitor_po_5_oeq), .olt(p2_magnitude_comparitor_po_5_olt));
  P2_Magnitude_Comparitor_PO p2_magnitude_comparitor_po_6 (
    .A(A[2]), .B(B[2]), .lgt(p2_magnitude_comparitor_po_5_ogt), .leq(p2_magnitude_comparitor_po_5_oeq),
    .llt(p2_magnitude_comparitor_po_5_olt), .ogt(p2_magnitude_comparitor_po_6_ogt),
    .oeq(p2_magnitude_comparitor_po_6_oeq), .olt(p2_magnitude_comparitor_po_6_olt));
  P2_Magnitude_Comparitor_PO p2_magnitude_comparitor_po_7 (
    .A(A[1]), .B(B[1]), .lgt(p2_magnitude_comparitor_po_6_ogt), .leq(p2_magnitude_comparitor_po_6_oeq),
    .llt(p2_magnitude_comparitor_po_6_olt), .ogt(p2_magnitude_comparitor_po_7_ogt),
    .oeq(p2_magnitude_comparitor_po_7_oeq), .olt(p2_magnitude_comparitor_po_7_olt));
  P2_Magnitude_Comparitor_PO p2_magnitude_comparitor_po_8 (
    .A(A[0]), .B(B[0]), .lgt(p2_magnitude_comparitor_po_7_ogt), .leq(p2_magnitude_comparitor_po_7_oeq),
    .llt(p2_magnitude_comparitor_po_7_olt), .ogt(Greater), .oeq(Equal), .olt(Less));
endmodule

module P2_Magnitude_Comparitor_PO (
  input  A,
  input  B,
  input  lgt,
  input  leq,
  input  llt,
  output ogt,
  output oeq,
  output olt
);

  wire and_1_out, and_2_out, not_1_out, not_2_out, xnor_1_out;

  not not_1 (not_1_out, A);
  not not_2 (not_2_out, B);
  and and_1 (and_1_out, A, not_2_out, leq);
  xnor xnor_1 (xnor_1_out, A, B);
  and and_2 (and_2_out, not_1_out, B, leq);
  or or_1 (ogt, and_1_out, lgt);
  and and_3 (oeq, leq, xnor_1_out);
  or or_2 (olt, and_2_out, llt);
endmodule

module P2_1_bit_Adder_PO (
  input  A,
  input  B,
  input  Ci,
  output Co,
  output S
);

  wire and_1_out, and_2_out, and_3_out, xor_1_out;

  and and_1 (and_1_out, A, B);
  and and_2 (and_2_out, A, Ci);
  and and_3 (and_3_out, B, Ci);
  or or_1 (Co, and_1_out, and_2_out, and_3_out);
  xor xor_1 (xor_1_out, A, B);
  xor xor_2 (S, xor_1_out, Ci);
endmodule

module P2_L_Shifter_4_times_PO (
  input  [7:0] Data_in,
  input  X,
  output [7:0] Data_out
);

  Multiplexer multiplexer_1 (.in0(Data_in[7]), .in1(Data_in[3]), .out(Data_out[7]), .sel(X));
  Multiplexer multiplexer_2 (.in0(Data_in[6]), .in1(Data_in[2]), .out(Data_out[6]), .sel(X));
  Multiplexer multiplexer_3 (.in0(Data_in[5]), .in1(Data_in[1]), .out(Data_out[5]), .sel(X));
  Multiplexer multiplexer_4 (.in0(Data_in[4]), .in1(Data_in[0]), .out(Data_out[4]), .sel(X));
  Multiplexer multiplexer_5 (.in0(Data_in[3]), .in1(1'b0), .out(Data_out[3]), .sel(X));
  Multiplexer multiplexer_6 (.in0(Data_in[2]), .in1(1'b0), .out(Data_out[2]), .sel(X));
  Multiplexer multiplexer_7 (.in0(Data_in[1]), .in1(1'b0), .out(Data_out[1]), .sel(X));
  Multiplexer multiplexer_8 (.in0(Data_in[0]), .in1(1'b0), .out(Data_out[0]), .sel(X));
endmodule

module P2_L_Shifter_2_times_PO (
  input  [7:0] Data_in,
  input  Y,
  output [7:0] Data_out
);

  Multiplexer multiplexer_1 (.in0(Data_in[7]), .in1(Data_in[5]), .out(Data_out[7]), .sel(Y));
  Multiplexer multiplexer_2 (.in0(Data_in[6]), .in1(Data_in[4]), .out(Data_out[6]), .sel(Y));
  Multiplexer multiplexer_3 (.in0(Data_in[5]), .in1(Data_in[3]), .out(Data_out[5]), .sel(Y));
  Multiplexer multiplexer_4 (.in0(Data_in[4]), .in1(Data_in[2]), .out(Data_out[4]), .sel(Y));
  Multiplexer multiplexer_5 (.in0(Data_in[3]), .in1(Data_in[1]), .out(Data_out[3]), .sel(Y));
  Multiplexer multiplexer_6 (.in0(Data_in[2]), .in1(Data_in[0]), .out(Data_out[2]), .sel(Y));
  Multiplexer multiplexer_7 (.in0(Data_in[1]), .in1(1'b0), .out(Data_out[1]), .sel(Y));
  Multiplexer multiplexer_8 (.in0(Data_in[0]), .in1(1'b0), .out(Data_out[0]), .sel(Y));
endmodule

module P2_L_Shifter_1_times_PO (
  input  [7:0] Data_in,
  input  Z,
  output [7:0] Data_out
);

  Multiplexer multiplexer_1 (.in0(Data_in[7]), .in1(Data_in[6]), .out(Data_out[7]), .sel(Z));
  Multiplexer multiplexer_2 (.in0(Data_in[6]), .in1(Data_in[5]), .out(Data_out[6]), .sel(Z));
  Multiplexer multiplexer_3 (.in0(Data_in[5]), .in1(Data_in[4]), .out(Data_out[5]), .sel(Z));
  Multiplexer multiplexer_4 (.in0(Data_in[4]), .in1(Data_in[3]), .out(Data_out[4]), .sel(Z));
  Multiplexer multiplexer_5 (.in0(Data_in[3]), .in1(Data_in[2]), .out(Data_out[3]), .sel(Z));
  Multiplexer multiplexer_6 (.in0(Data_in[2]), .in1(Data_in[1]), .out(Data_out[2]), .sel(Z));
  Multiplexer multiplexer_7 (.in0(Data_in[1]), .in1(Data_in[0]), .out(Data_out[1]), .sel(Z));
  Multiplexer multiplexer_8 (.in0(Data_in[0]), .in1(1'b0), .out(Data_out[0]), .sel(Z));
endmodule

module Memory_OT (
  input  [7:0] Control_In,
  input  [7:0] Address_In,
  input  [7:0] Databus_In,
  input  Enable,
  input  Clk,
  output [7:0] Databus_out,
  output Databus_control
);

  wire comparator_1_eq, comparator_2_eq, comparator_3_eq, or_1_out;
  wire [7:0] multiplexer_1_out, portio_1_p3, portio_2_p3, ram_1_dout, rom_1_data;

  Comparator comparator_1 (.a(8'h1), .b(Control_In), .eq(comparator_1_eq));  // open: gt, lt
  Comparator comparator_2 (.a(8'h2), .b(Control_In), .eq(comparator_2_eq));  // open: gt, lt
  Comparator comparator_3 (.a(8'h3), .b(Control_In), .eq(comparator_3_eq));  // open: gt, lt
  ROM rom_1 (.addr(portio_1_p3), .data(rom_1_data));
  // PortIO portio_1: pin names not known; wires that end beside it: comparator_1_eq, Address_In, portio_1_p3
  or or_1 (or_1_out, comparator_1_eq, comparator_2_eq);
  RAM ram_1 (
    .addr(Address_In), .we(comparator_3_eq), .oe(comparator_2_eq), .clk(Clk), .din(Databus_In),
    .dout(ram_1_dout));
  // PortIO portio_2: pin names not known; wires that end beside it: comparator_2_eq, ram_1_dout, portio_2_p3
  Multiplexer #(.width(8)) multiplexer_1 (
    .in0(portio_2_p3), .in1(rom_1_data), .out(multiplexer_1_out), .sel(comparator_1_eq));
  and and_1 (Databus_control, or_1_out, Enable);
  Register #(.trigger("high")) register_1 (.D(multiplexer_1_out), .clk(Clk), .Q(Databus_out));  // open: en, clr

  // Notes on the sheet:
  //   contents of rom_1 (hex, n*v repeats v):
  //   df 22 24 23 12*0 42 35 da 21 12*0 ff 2d 23 23 12*0 d 22 2c
endmodule

module MySubtractor_OT (
  input  in_1,
  input  [7:0] A,
  input  [7:0] B,
  output [7:0] C
);

  wire [7:0] not_1_out;

  assign not_1_out = ~B;  // NOT_Gate not_1, 8 bits wide
  MyAdder_OT myadder_ot_1 (.Cin(in_1), .A(A), .B(not_1_out), .C(C));  // open: cout
endmodule

module MyAdder_OT (
  input  Cin,
  input  [7:0] A,
  input  [7:0] B,
  output [7:0] C,
  output cout
);

  wire onebitadd_ot_1_cout, onebitadd_ot_2_cout, onebitadd_ot_3_cout, onebitadd_ot_4_cout,
       onebitadd_ot_5_cout, onebitadd_ot_6_cout, onebitadd_ot_7_cout;

  OneBitAdd_OT onebitadd_ot_1 (.cin(Cin), .a(A[0]), .b(B[0]), .s(C[0]), .cout(onebitadd_ot_1_cout));
  OneBitAdd_OT onebitadd_ot_2 (.cin(onebitadd_ot_1_cout), .a(A[1]), .b(B[1]), .s(C[1]), .cout(onebitadd_ot_2_cout));
  OneBitAdd_OT onebitadd_ot_3 (.cin(onebitadd_ot_2_cout), .a(A[2]), .b(B[2]), .s(C[2]), .cout(onebitadd_ot_3_cout));
  OneBitAdd_OT onebitadd_ot_4 (.cin(onebitadd_ot_3_cout), .a(A[3]), .b(B[3]), .s(C[3]), .cout(onebitadd_ot_4_cout));
  OneBitAdd_OT onebitadd_ot_5 (.cin(onebitadd_ot_4_cout), .a(A[4]), .b(B[4]), .s(C[4]), .cout(onebitadd_ot_5_cout));
  OneBitAdd_OT onebitadd_ot_6 (.cin(onebitadd_ot_5_cout), .a(A[5]), .b(B[5]), .s(C[5]), .cout(onebitadd_ot_6_cout));
  OneBitAdd_OT onebitadd_ot_7 (.cin(onebitadd_ot_6_cout), .a(A[6]), .b(B[6]), .s(C[6]), .cout(onebitadd_ot_7_cout));
  OneBitAdd_OT onebitadd_ot_8 (.cin(onebitadd_ot_7_cout), .a(A[7]), .b(B[7]), .s(C[7]), .cout(cout));
endmodule

module MyBarrelShifter_OT (
  input  [7:0] EightBitInput,
  input  [2:0] XYZ,
  output [7:0] EightBitOuput
);

  wire [7:0] fourbitshift_ot_1_afterfourshift, twobitshift_ot_1_aftertwoshift;

  FourBitShift_OT fourbitshift_ot_1 (
    .Data(EightBitInput), .X(XYZ[2]), .AfterFourShift(fourbitshift_ot_1_afterfourshift));  // open: Zero
  TwoBitShift_OT twobitshift_ot_1 (
    .Data(fourbitshift_ot_1_afterfourshift), .Y(XYZ[1]), .AfterTwoShift(twobitshift_ot_1_aftertwoshift));  // open: Zero
  OneBitShift_OT onebitshift_ot_1 (
    .Data(twobitshift_ot_1_aftertwoshift), .Z(XYZ[0]), .AfterOneShift(EightBitOuput));  // open: Zero
endmodule

module MyMagComparator_OT (
  input  lgt,
  input  leq,
  input  llt,
  input  [7:0] A,
  input  [7:0] B,
  output AgtB,
  output AeqB,
  output AltB
);

  wire comp_ot_1_next_aeqb, comp_ot_1_next_agtb, comp_ot_1_next_altb, comp_ot_2_next_aeqb,
       comp_ot_2_next_agtb, comp_ot_2_next_altb, comp_ot_3_next_aeqb, comp_ot_3_next_agtb,
       comp_ot_3_next_altb, comp_ot_4_next_aeqb, comp_ot_4_next_agtb, comp_ot_4_next_altb,
       comp_ot_5_next_aeqb, comp_ot_5_next_agtb, comp_ot_5_next_altb, comp_ot_6_next_aeqb,
       comp_ot_6_next_agtb, comp_ot_6_next_altb, comp_ot_7_next_aeqb, comp_ot_7_next_agtb,
       comp_ot_7_next_altb;

  Comp_OT comp_ot_1 (
    .P_AgtB(lgt), .P_AeqB(leq), .P_AltB(llt), .a(A[0]), .b(B[0]), .Next_AgtB(comp_ot_1_next_agtb),
    .Next_AeqB(comp_ot_1_next_aeqb), .Next_AltB(comp_ot_1_next_altb));
  Comp_OT comp_ot_2 (
    .P_AgtB(comp_ot_7_next_agtb), .P_AeqB(comp_ot_7_next_aeqb), .P_AltB(comp_ot_7_next_altb), .a(A[4]),
    .b(B[4]), .Next_AgtB(comp_ot_2_next_agtb), .Next_AeqB(comp_ot_2_next_aeqb),
    .Next_AltB(comp_ot_2_next_altb));
  Comp_OT comp_ot_3 (
    .P_AgtB(comp_ot_1_next_agtb), .P_AeqB(comp_ot_1_next_aeqb), .P_AltB(comp_ot_1_next_altb), .a(A[1]),
    .b(B[1]), .Next_AgtB(comp_ot_3_next_agtb), .Next_AeqB(comp_ot_3_next_aeqb),
    .Next_AltB(comp_ot_3_next_altb));
  Comp_OT comp_ot_4 (
    .P_AgtB(comp_ot_2_next_agtb), .P_AeqB(comp_ot_2_next_aeqb), .P_AltB(comp_ot_2_next_altb), .a(A[5]),
    .b(B[5]), .Next_AgtB(comp_ot_4_next_agtb), .Next_AeqB(comp_ot_4_next_aeqb),
    .Next_AltB(comp_ot_4_next_altb));
  Comp_OT comp_ot_5 (
    .P_AgtB(comp_ot_3_next_agtb), .P_AeqB(comp_ot_3_next_aeqb), .P_AltB(comp_ot_3_next_altb), .a(A[2]),
    .b(B[2]), .Next_AgtB(comp_ot_5_next_agtb), .Next_AeqB(comp_ot_5_next_aeqb),
    .Next_AltB(comp_ot_5_next_altb));
  Comp_OT comp_ot_6 (
    .P_AgtB(comp_ot_4_next_agtb), .P_AeqB(comp_ot_4_next_aeqb), .P_AltB(comp_ot_4_next_altb), .a(A[6]),
    .b(B[6]), .Next_AgtB(comp_ot_6_next_agtb), .Next_AeqB(comp_ot_6_next_aeqb),
    .Next_AltB(comp_ot_6_next_altb));
  Comp_OT comp_ot_7 (
    .P_AgtB(comp_ot_5_next_agtb), .P_AeqB(comp_ot_5_next_aeqb), .P_AltB(comp_ot_5_next_altb), .a(A[3]),
    .b(B[3]), .Next_AgtB(comp_ot_7_next_agtb), .Next_AeqB(comp_ot_7_next_aeqb),
    .Next_AltB(comp_ot_7_next_altb));
  Comp_OT comp_ot_8 (
    .P_AgtB(comp_ot_6_next_agtb), .P_AeqB(comp_ot_6_next_aeqb), .P_AltB(comp_ot_6_next_altb), .a(A[7]),
    .b(B[7]), .Next_AgtB(AgtB), .Next_AeqB(AeqB), .Next_AltB(AltB));
endmodule

module OneBitAdd_OT (
  input  cin,
  input  a,
  input  b,
  output s,
  output cout
);

  wire and_1_out, and_2_out, and_3_out, xor_1_out;

  xor xor_1 (xor_1_out, cin, b);
  and and_1 (and_1_out, cin, a);
  and and_2 (and_2_out, cin, b);
  and and_3 (and_3_out, a, b);
  xor xor_2 (s, xor_1_out, a);
  or or_1 (cout, and_1_out, and_2_out, and_3_out);
endmodule

module FourBitShift_OT (
  input  [7:0] Data,
  input  Zero,
  input  X,
  output [7:0] AfterFourShift
);

  Multiplexer multiplexer_1 (.in0(Data[7]), .in1(Data[3]), .out(AfterFourShift[7]), .sel(X));
  Multiplexer multiplexer_2 (.in0(Data[6]), .in1(Data[2]), .out(AfterFourShift[6]), .sel(X));
  Multiplexer multiplexer_3 (.in0(Data[5]), .in1(Data[1]), .out(AfterFourShift[5]), .sel(X));
  Multiplexer multiplexer_4 (.in0(Data[4]), .in1(Data[0]), .out(AfterFourShift[4]), .sel(X));
  Multiplexer multiplexer_5 (.in0(Data[3]), .in1(Zero), .out(AfterFourShift[3]), .sel(X));
  Multiplexer multiplexer_6 (.in0(Data[2]), .in1(Zero), .out(AfterFourShift[2]), .sel(X));
  Multiplexer multiplexer_7 (.in0(Data[1]), .in1(Zero), .out(AfterFourShift[1]), .sel(X));
  Multiplexer multiplexer_8 (.in0(Data[0]), .in1(Zero), .out(AfterFourShift[0]), .sel(X));
endmodule

module TwoBitShift_OT (
  input  [7:0] Data,
  input  Zero,
  input  Y,
  output [7:0] AfterTwoShift
);

  Multiplexer multiplexer_1 (.in0(Data[7]), .in1(Data[5]), .out(AfterTwoShift[7]), .sel(Y));
  Multiplexer multiplexer_2 (.in0(Data[6]), .in1(Data[4]), .out(AfterTwoShift[6]), .sel(Y));
  Multiplexer multiplexer_3 (.in0(Data[5]), .in1(Data[3]), .out(AfterTwoShift[5]), .sel(Y));
  Multiplexer multiplexer_4 (.in0(Data[4]), .in1(Data[2]), .out(AfterTwoShift[4]), .sel(Y));
  Multiplexer multiplexer_5 (.in0(Data[3]), .in1(Data[1]), .out(AfterTwoShift[3]), .sel(Y));
  Multiplexer multiplexer_6 (.in0(Data[2]), .in1(Data[0]), .out(AfterTwoShift[2]), .sel(Y));
  Multiplexer multiplexer_7 (.in0(Data[1]), .in1(Zero), .out(AfterTwoShift[1]), .sel(Y));
  Multiplexer multiplexer_8 (.in0(Data[0]), .in1(Zero), .out(AfterTwoShift[0]), .sel(Y));
endmodule

module OneBitShift_OT (
  input  [7:0] Data,
  input  Zero,
  input  Z,
  output [7:0] AfterOneShift
);

  Multiplexer multiplexer_1 (.in0(Data[7]), .in1(Data[6]), .out(AfterOneShift[7]), .sel(Z));
  Multiplexer multiplexer_2 (.in0(Data[6]), .in1(Data[5]), .out(AfterOneShift[6]), .sel(Z));
  Multiplexer multiplexer_3 (.in0(Data[5]), .in1(Data[4]), .out(AfterOneShift[5]), .sel(Z));
  Multiplexer multiplexer_4 (.in0(Data[4]), .in1(Data[3]), .out(AfterOneShift[4]), .sel(Z));
  Multiplexer multiplexer_5 (.in0(Data[3]), .in1(Data[2]), .out(AfterOneShift[3]), .sel(Z));
  Multiplexer multiplexer_6 (.in0(Data[2]), .in1(Data[1]), .out(AfterOneShift[2]), .sel(Z));
  Multiplexer multiplexer_7 (.in0(Data[1]), .in1(Data[0]), .out(AfterOneShift[1]), .sel(Z));
  Multiplexer multiplexer_8 (.in0(Data[0]), .in1(Zero), .out(AfterOneShift[0]), .sel(Z));
endmodule

module Comp_OT (
  input  P_AgtB,
  input  P_AeqB,
  input  P_AltB,
  input  a,
  input  b,
  output Next_AgtB,
  output Next_AeqB,
  output Next_AltB
);

  wire and_1_out, and_2_out, and_3_out, and_5_out, and_6_out, not_1_out, not_2_out, not_3_out, not_4_out,
       not_5_out, not_6_out, xor_1_out;

  and and_1 (and_1_out, P_AgtB, not_3_out, not_5_out);
  Multiplexer multiplexer_1 (.in0(and_2_out), .in1(and_1_out), .out(Next_AgtB), .sel(not_3_out));
  not not_1 (not_1_out, b);
  and and_2 (and_2_out, a, not_1_out, xor_1_out);
  not not_2 (not_2_out, P_AgtB);
  not not_3 (not_3_out, P_AeqB);
  and and_3 (and_3_out, not_2_out, P_AeqB, not_5_out);
  xor xor_1 (xor_1_out, a, b);
  not not_4 (not_4_out, xor_1_out);
  and and_4 (Next_AeqB, not_4_out, and_3_out);
  not not_5 (not_5_out, P_AltB);
  not not_6 (not_6_out, a);
  and and_5 (and_5_out, xor_1_out, not_6_out, b);
  and and_6 (and_6_out, not_2_out, not_3_out, P_AltB);
  Multiplexer multiplexer_2 (.in0(and_5_out), .in1(and_6_out), .out(Next_AltB), .sel(not_3_out));
endmodule

module EightBitFlipFlop_OT (
  input  [7:0] Data,
  input  CLK,
  output [7:0] Data_out
);

  D_Flip_Flop d_ff_1 (.D(Data[0]), .clk(CLK), .Q(Data_out[0]));  // open: Qn, preset, reset
  D_Flip_Flop d_ff_2 ();  // open: D, clk, Q, Qn, preset, reset
  D_Flip_Flop d_ff_3 (.D(Data[1]), .clk(CLK), .Q(Data_out[1]));  // open: Qn, preset, reset
  D_Flip_Flop d_ff_4 ();  // open: D, clk, Q, Qn, preset, reset
  D_Flip_Flop d_ff_5 (.D(Data[2]), .clk(CLK), .Q(Data_out[2]));  // open: Qn, preset, reset
  D_Flip_Flop d_ff_6 ();  // open: D, clk, Q, Qn, preset, reset
  D_Flip_Flop d_ff_7 (.D(Data[3]), .clk(CLK), .Q(Data_out[3]));  // open: Qn, preset, reset
  D_Flip_Flop d_ff_8 (.Qn(Data_out[4]));  // open: D, clk, Q, preset, reset
  D_Flip_Flop d_ff_9 (.D(Data[4]), .clk(CLK), .Q(Data_out[4]));  // open: Qn, preset, reset
  D_Flip_Flop d_ff_10 ();  // open: D, clk, Q, Qn, preset, reset
  D_Flip_Flop d_ff_11 (.D(Data[5]), .clk(CLK), .Q(Data_out[5]));  // open: Qn, preset, reset
  D_Flip_Flop d_ff_12 ();  // open: D, clk, Q, Qn, preset, reset
  D_Flip_Flop d_ff_13 (.D(Data[6]), .clk(CLK), .Q(Data_out[6]));  // open: Qn, preset, reset
  D_Flip_Flop d_ff_14 ();  // open: D, clk, Q, Qn, preset, reset
  D_Flip_Flop d_ff_15 (.D(Data[7]), .clk(CLK), .Q(Data_out[7]));  // open: Qn, preset, reset
  D_Flip_Flop d_ff_16 ();  // open: D, clk, Q, Qn, preset, reset
endmodule
