// Logisim project Lab_4_Circuit.circ as structural Verilog: 14 circuits, main circuit main
module main (
  input  [7:0] in_1,
  input  [7:0] in_2,
  input  [7:0] in_3,
  input  [7:0] in_4,
  input  [7:0] in_5,
  input  [7:0] in_6,
  output [7:0] out_7,
  output [7:0] out_8,
  output [7:0] out_9,
  output [7:0] out_10
);

  wire clock_1_out;
  wire [7:0] fakecpu_1_addressout, fakecpu_1_controlout, fakecpu_1_databusout, inputmodule_1_databus_out,
       memory_1_databus_out, portio_1_p2;

  Clock clock_1 (.out(clock_1_out));
  InputModule inputmodule_1 (
    .Control_In(fakecpu_1_controlout), .Address_In(fakecpu_1_addressout), .Input_1(in_3), .Input_2(in_4),
    .Input_3(in_5), .Input_4(in_6), .Clk(clock_1_out), .Databus_out(inputmodule_1_databus_out));  // open: Enable, Databus_control
  // PortIO portio_1: pin names not known; wires that end beside it: inputmodule_1_databus_out, portio_1_p2
  FakeCpu fakecpu_1 (
    .logicSignal(in_1), .AddressSignal(in_2), .DataBusIn(portio_1_p2), .Clk(clock_1_out),
    .ControlOut(fakecpu_1_controlout), .AddressOut(fakecpu_1_addressout), .DataBusOut(fakecpu_1_databusout));  // open: DatabusWrite
  // PortIO portio_2: pin names not known; wires that end beside it: fakecpu_1_databusout, portio_1_p2
  Memory memory_1 (
    .Control_In(fakecpu_1_controlout), .Address_In(fakecpu_1_addressout), .Databus_In(portio_1_p2),
    .Clk(clock_1_out), .Databus_out(memory_1_databus_out));  // open: Databus_control
  // PortIO portio_3: pin names not known; wires that end beside it: memory_1_databus_out, portio_1_p2
  OutputModule outputmodule_1 (
    .Control_In(fakecpu_1_controlout), .Address_In(fakecpu_1_addressout), .Databus_In(portio_1_p2),
    .Clk(clock_1_out), .Output_1(out_7), .Output_2(out_8), .Output_3(out_9), .Output_4(out_10));  // open: Enable
endmodule

module FakeCpu (
  input  [7:0] logicSignal,
  input  [7:0] AddressSignal,
  input  [7:0] DataBusIn,
  input  Clk,
  output [7:0] ControlOut,
  output [7:0] AddressOut,
  output [7:0] DataBusOut,
  output DatabusWrite
);
endmodule

module Memory (
  input  [7:0] Control_In,
  input  [7:0] Address_In,
  input  [7:0] Databus_In,
  input  Clk,
  output [7:0] Databus_out,
  output Databus_control
);
endmodule

module OutputModule (
  input  Enable,
  input  [7:0] Control_In,
  input  [7:0] Address_In,
  input  [7:0] Databus_In,
  input  Clk,
  output [7:0] Output_1,
  output [7:0] Output_2,
  output [7:0] Output_3,
  output [7:0] Output_4
);

  wire and_1_out, and_2_out, comparator_1_eq, demultiplexer_1_out0, demultiplexer_1_out1,
       demultiplexer_1_out2, demultiplexer_1_out3, nor_1_out;
  wire [7:0] controlled_buffer_1_out, controlled_buffer_2_out, controlled_buffer_3_out,
       controlled_buffer_4_out, demultiplexer_2_out0, demultiplexer_2_out1, demultiplexer_2_out2,
       demultiplexer_2_out3, p2_subtractor_1_s;

  Comparator comparator_1 (.a(8'h5), .b(Control_In), .eq(comparator_1_eq));  // open: gt, lt
  and and_1 (and_1_out, Enable, comparator_1_eq);
  P2_Subtractor p2_subtractor_1 (.A(Address_In), .B(8'h5), .S(p2_subtractor_1_s));
  nor nor_1 (nor_1_out, p2_subtractor_1_s[7], p2_subtractor_1_s[6], p2_subtractor_1_s[5], p2_subtractor_1_s[4], p2_subtractor_1_s[3], p2_subtractor_1_s[2]);
  and and_2 (and_2_out, and_1_out, nor_1_out);
  Demultiplexer #(.select(2)) demultiplexer_1 (
    .out0(demultiplexer_1_out0), .out1(demultiplexer_1_out1), .out2(demultiplexer_1_out2),
    .out3(demultiplexer_1_out3), .in(and_2_out), .sel(p2_subtractor_1_s[1:0]));
  Demultiplexer #(.select(2), .width(8)) demultiplexer_2 (
    .out0(demultiplexer_2_out0), .out1(demultiplexer_2_out1), .out2(demultiplexer_2_out2),
    .out3(demultiplexer_2_out3), .in(Databus_In), .sel(p2_subtractor_1_s[1:0]));
  assign controlled_buffer_1_out = demultiplexer_1_out0 ? demultiplexer_2_out0 : 8'bz;  // Controlled_Buffer controlled_buffer_1
  assign controlled_buffer_2_out = demultiplexer_1_out1 ? demultiplexer_2_out1 : 8'bz;  // Controlled_Buffer controlled_buffer_2
  assign controlled_buffer_3_out = demultiplexer_1_out2 ? demultiplexer_2_out2 : 8'bz;  // Controlled_Buffer controlled_buffer_3
  assign controlled_buffer_4_out = demultiplexer_1_out3 ? demultiplexer_2_out3 : 8'bz;  // Controlled_Buffer controlled_buffer_4
  Register register_1 (.D(controlled_buffer_1_out), .en(demultiplexer_1_out0), .clk(Clk), .Q(Output_1));  // open: clr
  Register register_2 (.D(controlled_buffer_2_out), .en(demultiplexer_1_out1), .clk(Clk), .Q(Output_2));  // open: clr
  Register register_3 (.D(controlled_buffer_3_out), .en(demultiplexer_1_out2), .clk(Clk), .Q(Output_3));  // open: clr
  Register register_4 (.D(controlled_buffer_4_out), .en(demultiplexer_1_out3), .clk(Clk), .Q(Output_4));  // open: clr
endmodule

module InputModule (
  input  [7:0] Control_In,
  input  [7:0] Address_In,
  input  [7:0] Input_1,
  input  [7:0] Input_2,
  input  [7:0] Input_3,
  input  [7:0] Input_4,
  input  Clk,
  input  Enable,
  output [7:0] Databus_out,
  output Databus_control
);

  wire and_1_out, comparator_1_eq, nor_1_out;
  wire [7:0] p2_subtractor_1_s, register_1_q, register_2_q, register_3_q, register_4_q;

  Comparator comparator_1 (.a(8'h4), .b(Control_In), .eq(comparator_1_eq));  // open: gt, lt
  P2_Subtractor p2_subtractor_1 (.A(Address_In), .B(8'h1), .S(p2_subtractor_1_s));
  nor nor_1 (nor_1_out, p2_subtractor_1_s[7], p2_subtractor_1_s[6], p2_subtractor_1_s[5], p2_subtractor_1_s[4], p2_subtractor_1_s[3], p2_subtractor_1_s[2]);
  and and_1 (and_1_out, nor_1_out, Enable);
  Register register_1 (.D(Input_1), .clk(Clk), .Q(register_1_q));  // open: en, clr
  Register register_2 (.D(Input_2), .clk(Clk), .Q(register_2_q));  // open: en, clr
  Register register_3 (.D(Input_3), .clk(Clk), .Q(register_3_q));  // open: en, clr
  Register register_4 (.D(Input_4), .clk(Clk), .Q(register_4_q));  // open: en, clr
  Multiplexer #(.select(2), .width(8)) multiplexer_1 (
    .in0(register_1_q), .in1(register_2_q), .in2(register_3_q), .in3(register_4_q), .out(Databus_out),
    .sel(p2_subtractor_1_s[1:0]));
  and and_2 (Databus_control, comparator_1_eq, and_1_out);

  // Notes on the sheet:
  //   This should be a good way to check if the control signal meets a certain condition/conditions
  //   change address system
endmodule

module P2_8_bit_Adder (
  input  Ci,
  input  [7:0] A,
  input  [7:0] B,
  output Co,
  output [7:0] S
);

  wire p2_1_bit_adder_1_co, p2_1_bit_adder_2_co, p2_1_bit_adder_3_co, p2_1_bit_adder_4_co,
       p2_1_bit_adder_5_co, p2_1_bit_adder_6_co, p2_1_bit_adder_7_co;

  P2_1_bit_Adder p2_1_bit_adder_1 (.A(A[0]), .B(B[0]), .Ci(Ci), .Co(p2_1_bit_adder_1_co), .S(S[0]));
  P2_1_bit_Adder p2_1_bit_adder_2 (.A(A[1]), .B(B[1]), .Ci(p2_1_bit_adder_1_co), .Co(p2_1_bit_adder_2_co), .S(S[1]));
  P2_1_bit_Adder p2_1_bit_adder_3 (.A(A[2]), .B(B[2]), .Ci(p2_1_bit_adder_2_co), .Co(p2_1_bit_adder_3_co), .S(S[2]));
  P2_1_bit_Adder p2_1_bit_adder_4 (.A(A[3]), .B(B[3]), .Ci(p2_1_bit_adder_3_co), .Co(p2_1_bit_adder_4_co), .S(S[3]));
  P2_1_bit_Adder p2_1_bit_adder_5 (.A(A[4]), .B(B[4]), .Ci(p2_1_bit_adder_4_co), .Co(p2_1_bit_adder_5_co), .S(S[4]));
  P2_1_bit_Adder p2_1_bit_adder_6 (.A(A[5]), .B(B[5]), .Ci(p2_1_bit_adder_5_co), .Co(p2_1_bit_adder_6_co), .S(S[5]));
  P2_1_bit_Adder p2_1_bit_adder_7 (.A(A[6]), .B(B[6]), .Ci(p2_1_bit_adder_6_co), .Co(p2_1_bit_adder_7_co), .S(S[6]));
  P2_1_bit_Adder p2_1_bit_adder_8 (.A(A[7]), .B(B[7]), .Ci(p2_1_bit_adder_7_co), .Co(Co), .S(S[7]));
endmodule

module P2_L_Shifter (
  input  [7:0] in_1,
  input  in_2,
  input  in_3,
  input  in_4,
  output [7:0] out_5
);

  wire [7:0] p2_l_shifter_2_times_1_data_out, p2_l_shifter_4_times_1_data_out;

  P2_L_Shifter_4_times p2_l_shifter_4_times_1 (.Data_in(in_1), .X(in_2), .Data_out(p2_l_shifter_4_times_1_data_out));
  P2_L_Shifter_2_times p2_l_shifter_2_times_1 (
    .Data_in(p2_l_shifter_4_times_1_data_out), .Y(in_3), .Data_out(p2_l_shifter_2_times_1_data_out));
  P2_L_Shifter_1_times p2_l_shifter_1_times_1 (.Data_in(p2_l_shifter_2_times_1_data_out), .Z(in_4), .Data_out(out_5));
endmodule

module P2_Subtractor (
  input  [7:0] A,
  input  [7:0] B,
  output [7:0] S
);

  wire [7:0] not_1_out;

  assign not_1_out = ~B;  // NOT_Gate not_1, 8 bits wide
  P2_8_bit_Adder p2_8_bit_adder_1 (.Ci(1'b1), .A(A), .B(not_1_out), .S(S));  // open: Co
endmodule

module P2_8_bit_Magnitude_Comparitor (
  input  [7:0] A,
  input  [7:0] B,
  output Greater,
  output Equal,
  output Less
);

  wire p2_magnitude_comparitor_1_oeq, p2_magnitude_comparitor_1_ogt, p2_magnitude_comparitor_1_olt,
       p2_magnitude_comparitor_2_oeq, p2_magnitude_comparitor_2_ogt, p2_magnitude_comparitor_2_olt,
       p2_magnitude_comparitor_3_oeq, p2_magnitude_comparitor_3_ogt, p2_magnitude_comparitor_3_olt,
       p2_magnitude_comparitor_4_oeq, p2_magnitude_comparitor_4_ogt, p2_magnitude_comparitor_4_olt,
       p2_magnitude_comparitor_5_oeq, p2_magnitude_comparitor_5_ogt, p2_magnitude_comparitor_5_olt,
       p2_magnitude_comparitor_6_oeq, p2_magnitude_comparitor_6_ogt, p2_magnitude_comparitor_6_olt,
       p2_magnitude_comparitor_7_oeq, p2_magnitude_comparitor_7_ogt, p2_magnitude_comparitor_7_olt;

  P2_Magnitude_Comparitor p2_magnitude_comparitor_1 (
    .A(A[7]), .B(B[7]), .lgt(1'b0), .leq(1'b1), .llt(1'b0), .ogt(p2_magnitude_comparitor_1_ogt),
    .oeq(p2_magnitude_comparitor_1_oeq), .olt(p2_magnitude_comparitor_1_olt));
  P2_Magnitude_Comparitor p2_magnitude_comparitor_2 (
    .A(A[6]), .B(B[6]), .lgt(p2_magnitude_comparitor_1_ogt), .leq(p2_magnitude_comparitor_1_oeq),
    .llt(p2_magnitude_comparitor_1_olt), .ogt(p2_magnitude_comparitor_2_ogt),
    .oeq(p2_magnitude_comparitor_2_oeq), .olt(p2_magnitude_comparitor_2_olt));
  P2_Magnitude_Comparitor p2_magnitude_comparitor_3 (
    .A(A[5]), .B(B[5]), .lgt(p2_magnitude_comparitor_2_ogt), .leq(p2_magnitude_comparitor_2_oeq),
    .llt(p2_magnitude_comparitor_2_olt), .ogt(p2_magnitude_comparitor_3_ogt),
    .oeq(p2_magnitude_comparitor_3_oeq), .olt(p2_magnitude_comparitor_3_olt));
  P2_Magnitude_Comparitor p2_magnitude_comparitor_4 (
    .A(A[4]), .B(B[4]), .lgt(p2_magnitude_comparitor_3_ogt), .leq(p2_magnitude_comparitor_3_oeq),
    .llt(p2_magnitude_comparitor_3_olt), .ogt(p2_magnitude_comparitor_4_ogt),
    .oeq(p2_magnitude_comparitor_4_oeq), .olt(p2_magnitude_comparitor_4_olt));
  P2_Magnitude_Comparitor p2_magnitude_comparitor_5 (
    .A(A[3]), .B(B[3]), .lgt(p2_magnitude_comparitor_4_ogt), .leq(p2_magnitude_comparitor_4_oeq),
    .llt(p2_magnitude_comparitor_4_olt), .ogt(p2_magnitude_comparitor_5_ogt),
    .oeq(p2_magnitude_comparitor_5_oeq), .olt(p2_magnitude_comparitor_5_olt));
  P2_Magnitude_Comparitor p2_magnitude_comparitor_6 (
    .A(A[2]), .B(B[2]), .lgt(p2_magnitude_comparitor_5_ogt), .leq(p2_magnitude_comparitor_5_oeq),
    .llt(p2_magnitude_comparitor_5_olt), .ogt(p2_magnitude_comparitor_6_ogt),
    .oeq(p2_magnitude_comparitor_6_oeq), .olt(p2_magnitude_comparitor_6_olt));
  P2_Magnitude_Comparitor p2_magnitude_comparitor_7 (
    .A(A[1]), .B(B[1]), .lgt(p2_magnitude_comparitor_6_ogt), .leq(p2_magnitude_comparitor_6_oeq),
    .llt(p2_magnitude_comparitor_6_olt), .ogt(p2_magnitude_comparitor_7_ogt),
    .oeq(p2_magnitude_comparitor_7_oeq), .olt(p2_magnitude_comparitor_7_olt));
  P2_Magnitude_Comparitor p2_magnitude_comparitor_8 (
    .A(A[0]), .B(B[0]), .lgt(p2_magnitude_comparitor_7_ogt), .leq(p2_magnitude_comparitor_7_oeq),
    .llt(p2_magnitude_comparitor_7_olt), .ogt(Greater), .oeq(Equal), .olt(Less));
endmodule

module P2_Magnitude_Comparitor (
  input  A,
  input  B,
  input  lgt,
  input  leq,
  input  llt,
  output ogt,
  output oeq,
  output olt
);

  wire and_1_out, and_2_out, not_1_out, not_2_out, xnor_1_out;

  not not_1 (not_1_out, A);
  not not_2 (not_2_out, B);
  and and_1 (and_1_out, A, not_2_out, leq);
  xnor xnor_1 (xnor_1_out, A, B);
  and and_2 (and_2_out, not_1_out, B, leq);
  or or_1 (ogt, and_1_out, lgt);
  and and_3 (oeq, leq, xnor_1_out);
  or or_2 (olt, and_2_out, llt);
endmodule

module P2_1_bit_Adder (
  input  A,
  input  B,
  input  Ci,
  output Co,
  output S
);

  wire and_1_out, and_2_out, and_3_out, xor_1_out;

  and and_1 (and_1_out, A, B);
  and and_2 (and_2_out, A, Ci);
  and and_3 (and_3_out, B, Ci);
  or or_1 (Co, and_1_out, and_2_out, and_3_out);
  xor xor_1 (xor_1_out, A, B);
  xor xor_2 (S, xor_1_out, Ci);
endmodule

module P2_L_Shifter_4_times (
  input  [7:0] Data_in,
  input  X,
  output [7:0] Data_out
);

  Multiplexer multiplexer_1 (.in0(Data_in[7]), .in1(Data_in[3]), .out(Data_out[7]), .sel(X));
  Multiplexer multiplexer_2 (.in0(Data_in[6]), .in1(Data_in[2]), .out(Data_out[6]), .sel(X));
  Multiplexer multiplexer_3 (.in0(Data_in[5]), .in1(Data_in[1]), .out(Data_out[5]), .sel(X));
  Multiplexer multiplexer_4 (.in0(Data_in[4]), .in1(Data_in[0]), .out(Data_out[4]), .sel(X));
  Multiplexer multiplexer_5 (.in0(Data_in[3]), .in1(1'b0), .out(Data_out[3]), .sel(X));
  Multiplexer multiplexer_6 (.in0(Data_in[2]), .in1(1'b0), .out(Data_out[2]), .sel(X));
  Multiplexer multiplexer_7 (.in0(Data_in[1]), .in1(1'b0), .out(Data_out[1]), .sel(X));
  Multiplexer multiplexer_8 (.in0(Data_in[0]), .in1(1'b0), .out(Data_out[0]), .sel(X));
endmodule

module P2_L_Shifter_2_times (
  input  [7:0] Data_in,
  input  Y,
  output [7:0] Data_out
);

  Multiplexer multiplexer_1 (.in0(Data_in[7]), .in1(Data_in[5]), .out(Data_out[7]), .sel(Y));
  Multiplexer multiplexer_2 (.in0(Data_in[6]), .in1(Data_in[4]), .out(Data_out[6]), .sel(Y));
  Multiplexer multiplexer_3 (.in0(Data_in[5]), .in1(Data_in[3]), .out(Data_out[5]), .sel(Y));
  Multiplexer multiplexer_4 (.in0(Data_in[4]), .in1(Data_in[2]), .out(Data_out[4]), .sel(Y));
  Multiplexer multiplexer_5 (.in0(Data_in[3]), .in1(Data_in[1]), .out(Data_out[3]), .sel(Y));
  Multiplexer multiplexer_6 (.in0(Data_in[2]), .in1(Data_in[0]), .out(Data_out[2]), .sel(Y));
  Multiplexer multiplexer_7 (.in0(Data_in[1]), .in1(1'b0), .out(Data_out[1]), .sel(Y));
  Multiplexer multiplexer_8 (.in0(Data_in[0]), .in1(1'b0), .out(Data_out[0]), .sel(Y));
endmodule

module P2_L_Shifter_1_times (
  input  [7:0] Data_in,
  input  Z,
  output [7:0] Data_out
);

  Multiplexer multiplexer_1 (.in0(Data_in[7]), .in1(Data_in[6]), .out(Data_out[7]), .sel(Z));
  Multiplexer multiplexer_2 (.in0(Data_in[6]), .in1(Data_in[5]), .out(Data_out[6]), .sel(Z));
  Multiplexer multiplexer_3 (.in0(Data_in[5]), .in1(Data_in[4]), .out(Data_out[5]), .sel(Z));
  Multiplexer multiplexer_4 (.in0(Data_in[4]), .in1(Data_in[3]), .out(Data_out[4]), .sel(Z));
  Multiplexer multiplexer_5 (.in0(Data_in[3]), .in1(Data_in[2]), .out(Data_out[3]), .sel(Z));
  Multiplexer multiplexer_6 (.in0(Data_in[2]), .in1(Data_in[1]), .out(Data_out[2]), .sel(Z));
  Multiplexer multiplexer_7 (.in0(Data_in[1]), .in1(Data_in[0]), .out(Data_out[1]), .sel(Z));
  Multiplexer multiplexer_8 (.in0(Data_in[0]), .in1(1'b0), .out(Data_out[0]), .sel(Z));
endmodule
