// Logisim project L6_MAIN.circ as structural Verilog: 33 circuits, main circuit main
module main (
);

  wire button_1_out, clock_1_out, clocktimingmodule_1_decodeclk, clocktimingmodule_1_executeclk,
       clocktimingmodule_1_fetchclk, clocktimingmodule_1_memclk, clocktimingmodule_1_pcupdateclk,
       clocktimingmodule_1_writebackclk, execute_1_cond_out, fetch_1_hlt;
  wire [3:0] fetch_1_icode, fetch_1_ifun, fetch_1_ra, fetch_1_rb;
  wire [63:0] decode_writeback_1_vala, decode_writeback_1_valb, execute_1_vale_out, fetch_1_valc,
       fetch_1_valp, memory_main_1_valm, pc_update_1_newpc, register_1_q;

  Clock clock_1 (.out(clock_1_out));
  Button button_1 (.out(button_1_out));
  Register #(.width(64)) register_1 (
    .D(pc_update_1_newpc), .clk(clocktimingmodule_1_pcupdateclk), .Q(register_1_q));  // open: en, clr
  ClockTimingModule clocktimingmodule_1 (
    .Clock(clock_1_out), .HLT(fetch_1_hlt), .Start(button_1_out), .FetchCLK(clocktimingmodule_1_fetchclk),
    .DecodeCLK(clocktimingmodule_1_decodeclk), .ExecuteCLK(clocktimingmodule_1_executeclk),
    .MemCLK(clocktimingmodule_1_memclk), .WriteBackCLK(clocktimingmodule_1_writebackclk),
    .PCUpdateClk(clocktimingmodule_1_pcupdateclk));  // open: Reset
  Fetch fetch_1 (
    .Clock(clocktimingmodule_1_fetchclk), .PC(register_1_q), .reset(clocktimingmodule_1_pcupdateclk),
    .icode(fetch_1_icode), .ifun(fetch_1_ifun), .rA(fetch_1_ra), .rB(fetch_1_rb), .valC(fetch_1_valc),
    .valP(fetch_1_valp), .HLT(fetch_1_hlt));  // open: instr_valid
  Decode_WriteBack decode_writeback_1 (
    .DecodeCLK(clocktimingmodule_1_decodeclk), .WBCLK(clocktimingmodule_1_writebackclk),
    .icode(fetch_1_icode), .rA(fetch_1_ra), .rB(fetch_1_rb), .ValM(memory_main_1_valm),
    .ValE(execute_1_vale_out), .valA(decode_writeback_1_vala), .valB(decode_writeback_1_valb));
  Execute execute_1 (
    .ValA(decode_writeback_1_vala), .ValB(decode_writeback_1_valb), .iCode(fetch_1_icode),
    .iFun(fetch_1_ifun), .ValC(fetch_1_valc), .clk(clocktimingmodule_1_executeclk),
    .ValE_Out(execute_1_vale_out), .cond_out(execute_1_cond_out));
  Memory_main memory_main_1 (
    .Val_E(execute_1_vale_out), .Val_P(fetch_1_valp), .icode(fetch_1_icode), .Val_A(decode_writeback_1_vala),
    .CLK(clocktimingmodule_1_memclk), .ValM(memory_main_1_valm));
  PC_Update pc_update_1 (
    .valP(fetch_1_valp), .JMP(execute_1_cond_out), .valC(fetch_1_valc), .valM(memory_main_1_valm),
    .icode(fetch_1_icode), .newPC(pc_update_1_newpc));
endmodule

module ClockTimingModule (
  input  Reset,
  input  Clock,
  input  HLT,
  input  Start,
  output FetchCLK,
  output DecodeCLK,
  output ExecuteCLK,
  output MemCLK,
  output WriteBackCLK,
  output PCUpdateClk
);

  wire and_1_out, multiplexer_1_out;
  wire [2:0] rom_1_data;
  wire [7:0] counter_1_q;

  Multiplexer multiplexer_1 (.in0(Clock), .in1(1'b0), .out(multiplexer_1_out), .sel(and_1_out));
  and and_1 (and_1_out, HLT, ~Start);  // AND_Gate
  Counter #(.max('h17)) counter_1 (
    .clr(Reset), .up(1'b1), .clk(multiplexer_1_out), .Q(counter_1_q));  // open: load, count, D, carry
  ROM #(.dataWidth(3)) rom_1 (.addr(counter_1_q), .data(rom_1_data));
  Demultiplexer #(.select(3)) demultiplexer_1 (
    .out1(FetchCLK), .out2(DecodeCLK), .out3(ExecuteCLK), .out4(MemCLK), .out5(WriteBackCLK),
    .out6(PCUpdateClk), .in(multiplexer_1_out), .sel(rom_1_data));  // open: out0, out7

  // Notes on the sheet:
  //   contents of rom_1 (hex, n*v repeats v):
  //   11*1 2 3 8*4 5 5 6
endmodule

module Fetch (
  input  Clock,
  input  [63:0] PC,
  input  reset,
  output instr_valid,
  output [3:0] icode,
  output [3:0] ifun,
  output [3:0] rA,
  output [3:0] rB,
  output [63:0] valC,
  output [63:0] valP,
  output HLT
);

  wire and_1_out;
  wire [7:0] instruction_memory_1_b0, instruction_memory_1_b1, instruction_memory_1_b2,
       instruction_memory_1_b3, instruction_memory_1_b4, instruction_memory_1_b5, instruction_memory_1_b6,
       instruction_memory_1_b7, instruction_memory_1_b8, instruction_memory_1_b9;

  Instruction_Memory instruction_memory_1 (
    .PC(PC), .Clock(Clock), .reset(reset), .b0(instruction_memory_1_b0), .b1(instruction_memory_1_b1),
    .b2(instruction_memory_1_b2), .b3(instruction_memory_1_b3), .b4(instruction_memory_1_b4),
    .b5(instruction_memory_1_b5), .b6(instruction_memory_1_b6), .b7(instruction_memory_1_b7),
    .b8(instruction_memory_1_b8), .b9(instruction_memory_1_b9));
  Register #(.trigger("falling"), .width(1)) register_1 (.D(and_1_out), .clk(Clock), .Q(HLT));  // open: en, clr
  and and_1 (and_1_out, ~instruction_memory_1_b0[4], ~instruction_memory_1_b0[5], ~instruction_memory_1_b0[6], ~instruction_memory_1_b0[7]);  // AND_Gate
  SplitAndAlign splitandalign_1 (
    .Enable(1'b1), .Byte0(instruction_memory_1_b0), .Byte1(instruction_memory_1_b1),
    .Byte2(instruction_memory_1_b2), .Byte3(instruction_memory_1_b3), .Byte4(instruction_memory_1_b4),
    .Byte5(instruction_memory_1_b5), .Byte6(instruction_memory_1_b6), .Byte7(instruction_memory_1_b7),
    .Byte8(instruction_memory_1_b8), .Byte9(instruction_memory_1_b9), .CurrPC_In(PC), .CLK(Clock),
    .iCode_Error(instr_valid), .iCode(icode), .iFun(ifun), .rA(rA), .rB(rB), .ValC(valC), .valP(valP));
endmodule

module Decode_WriteBack (
  input  DecodeCLK,
  input  WBCLK,
  input  [3:0] icode,
  input  [3:0] rA,
  input  [3:0] rB,
  input  [63:0] ValM,
  input  [63:0] ValE,
  output [63:0] valA,
  output [63:0] valB
);

  wire wb_clk_logic_1_w_e, wb_clk_logic_1_w_m;
  wire [3:0] srca_1_src, srcb_1_src, wb_dest_logic_1_deste;
  wire [63:0] register_file_1_vala, register_file_1_valb;

  srcA srca_1 (.icode(icode), .rA(rA), .src(srca_1_src));
  srcB srcb_1 (.icode(icode), .rB(rB), .src(srcb_1_src));
  WB_DEST_logic wb_dest_logic_1 (.Icode(icode), .iRB(rB), .DestE(wb_dest_logic_1_deste));
  WB_CLK_Logic wb_clk_logic_1 (.Icode(icode), .clk(WBCLK), .W_E(wb_clk_logic_1_w_e), .W_M(wb_clk_logic_1_w_m));
  Register_File register_file_1 (
    .valM(ValM), .valE(ValE), .dstE(wb_dest_logic_1_deste), .dstM(rA), .W_E(wb_clk_logic_1_w_e),
    .W_M(wb_clk_logic_1_w_m), .srcA(srca_1_src), .srcB(srcb_1_src), .WB_CLK(WBCLK),
    .valA(register_file_1_vala), .valB(register_file_1_valb));
  Register #(.width(64)) register_1 (.D(register_file_1_vala), .clk(DecodeCLK), .Q(valA));  // open: en, clr
  Register #(.width(64)) register_2 (.D(register_file_1_valb), .clk(DecodeCLK), .Q(valB));  // open: en, clr
endmodule

module Instruction_Memory (
  input  [63:0] PC,
  input  Clock,
  input  reset,
  output [7:0] b0,
  output [7:0] b1,
  output [7:0] b2,
  output [7:0] b3,
  output [7:0] b4,
  output [7:0] b5,
  output [7:0] b6,
  output [7:0] b7,
  output [7:0] b8,
  output [7:0] b9
);

  wire decoder_1_out0, decoder_1_out1, decoder_1_out2, decoder_1_out3, decoder_1_out4, decoder_1_out5,
       decoder_1_out6, decoder_1_out7, decoder_1_out8, decoder_1_out9;
  wire [3:0] counter_1_q;
  wire [7:0] rom_1_data;
  wire [11:0] adder_1_out;

  Counter #(.max('ha), .width(4)) counter_1 (
    .clr(reset), .count(Clock), .clk(Clock), .Q(counter_1_q));  // open: load, up, D, carry
  ROM #(.addrWidth(12)) rom_1 (.addr(adder_1_out), .data(rom_1_data));
  Adder #(.width(12)) adder_1 (.a(PC[11:0]), .b({{8{1'b0}}, counter_1_q}), .out(adder_1_out));  // open: cin, cout
  Decoder #(.select(4)) decoder_1 (
    .out0(decoder_1_out0), .out1(decoder_1_out1), .out2(decoder_1_out2), .out3(decoder_1_out3),
    .out4(decoder_1_out4), .out5(decoder_1_out5), .out6(decoder_1_out6), .out7(decoder_1_out7),
    .out8(decoder_1_out8), .out9(decoder_1_out9), .sel(counter_1_q));  // open: out10, out11, out12, out13, out14, out15, en
  Register register_1 (.D(rom_1_data), .en(decoder_1_out0), .clk(Clock), .Q(b0));  // open: clr
  Register register_2 (.D(rom_1_data), .en(decoder_1_out1), .clk(Clock), .Q(b1));  // open: clr
  Register register_3 (.D(rom_1_data), .en(decoder_1_out2), .clk(Clock), .Q(b2));  // open: clr
  Register register_4 (.D(rom_1_data), .en(decoder_1_out3), .clk(Clock), .Q(b3));  // open: clr
  Register register_5 (.D(rom_1_data), .en(decoder_1_out4), .clk(Clock), .Q(b4));  // open: clr
  Register register_6 (.D(rom_1_data), .en(decoder_1_out5), .clk(Clock), .Q(b5));  // open: clr
  Register register_7 (.D(rom_1_data), .en(decoder_1_out6), .clk(Clock), .Q(b6));  // open: clr
  Register register_8 (.D(rom_1_data), .en(decoder_1_out7), .clk(Clock), .Q(b7));  // open: clr
  Register register_9 (.D(rom_1_data), .en(decoder_1_out8), .clk(Clock), .Q(b8));  // open: clr
  Register register_10 (.D(rom_1_data), .en(decoder_1_out9), .clk(Clock), .Q(b9));  // open: clr

  // Notes on the sheet:
  //   contents of rom_1 (hex, n*v repeats v):
  //   30 f4 f0 f 6*0 80 14 8*0 30 f0 a0 4 6*0 30 f7 10 7*0 30 f3 8 7*0 30 fe 1 7*0 30 f8 a0 6 6*0 30 f9 e0
  //   6 6*0 80 29 1 6*0 80 84 1 6*0 80 6c 7*0 90 20 8a 30 fc 2 7*0 80 82 7*0 90 20 9b 30 fd 2 7*0 80 a5
  //   7*0 60 7a 61 ec 76 82 7*0 90 a0 f a0 af a0 bf 50 a 8*0 50 6b 8*0 80 d 1 6*0 20 1 60 3a 60 7b 50 a
  //   8*0 50 6b 8*0 80 d 1 6*0 60 1 b0 bf b0 af b0 f 40 10 8*0 60 30 60 3b 61 ed 76 a5 7*0 90 20 2 61 e6
  //   76 1b 1 6*0 90 60 20 61 e6 76 1b 1 6*0 90 a0 8f 30 f2 1 7*0 40 28 8*0 60 38 30 f2 10 7*0 40 28 8*0
  //   60 38 30 f2 10 7*0 40 28 8*0 60 38 30 f2 20 7*0 40 28 8*0 b0 8f 90 a0 9f 30 f2 40 7*0 40 29 8*0 60
  //   39 30 f2 10 7*0 40 29 8*0 60 39 30 f2 20 7*0 40 29 8*0 60 39 30 f2 1 7*0 40 29 8*0 b0 9f 90
endmodule

module Reg_Enable (
  input  [3:0] iCode_inp,
  output T_Reg
);

  wire aBc_out, aCd_out, bC_out, eight_a_out, four_b_out, one_d_out, two_c_out;

  not eight_a (eight_a_out, iCode_inp[3]);
  not four_b (four_b_out, iCode_inp[2]);
  not two_c (two_c_out, iCode_inp[1]);
  not one_d (one_d_out, iCode_inp[0]);
  and aBc (aBc_out, eight_a_out, iCode_inp[2], two_c_out);
  and bC (bC_out, four_b_out, iCode_inp[1]);
  and aCd (aCd_out, eight_a_out, iCode_inp[1], one_d_out);
  or or_1 (T_Reg, aBc_out, bC_out, aCd_out);

  // Notes on the sheet:
  //   This Module is to determine which op needs rA/rB
endmodule

module Split (
  input  [7:0] Byte_0_INP,
  input  Enable,
  input  Clk,
  output INP_Error,
  output [3:0] iCode,
  output [3:0] iFun
);

  wire comparator_1_eq, comparator_1_lt;

  Register #(.width(4)) register_1 (.D(Byte_0_INP[7:4]), .en(Enable), .clk(Clk), .Q(iCode));  // open: clr
  Register #(.width(4)) register_2 (.D(Byte_0_INP[3:0]), .en(Enable), .clk(Clk), .Q(iFun));  // open: clr
  Comparator #(.mode("unsigned"), .width(4)) comparator_1 (
    .a(4'b1100), .b(iCode), .eq(comparator_1_eq), .lt(comparator_1_lt));  // open: gt
  or or_1 (INP_Error, comparator_1_lt, comparator_1_eq);

  // Notes on the sheet:
  //   compare if iCode >= 12
  //   pass in new data when iCode < 12
  //   This Module is to split first bit 0 to iCode and iFun
  //   maintain Original Val
endmodule

module Align_Old (
  input  NeedReg_In,
  input  NeedValC_In,
  input  Clk,
  input  [3:0] Byte_0_iCode,
  input  [7:0] Byte_1_rA_rB,
  input  [7:0] Byte_2_Inp,
  input  [7:0] Byte_3_Inp,
  input  [7:0] Byte_4_Inp,
  input  [7:0] Byte_5_Inp,
  input  [7:0] Byte_6_Inp,
  input  [7:0] Byte_7_Inp,
  input  [7:0] Byte_8_Inp,
  input  [7:0] Byte_9_Inp,
  output [3:0] rA,
  output [3:0] rB,
  output [63:0] ValC
);

  wire aBc_out, Abcd_out, aCD_out, not_1_out, not_2_out, not_3_out, not_4_out, or_1_out;
  wire [63:0] Byte_2_q;

  not not_1 (not_1_out, Byte_0_iCode[3]);
  not not_2 (not_2_out, Byte_0_iCode[1]);
  not not_3 (not_3_out, Byte_0_iCode[2]);
  not not_4 (not_4_out, Byte_0_iCode[0]);
  and Abcd (Abcd_out, Byte_0_iCode[3], not_3_out, not_2_out, not_4_out, NeedValC_In);
  and aBc (aBc_out, not_1_out, Byte_0_iCode[2], not_2_out, NeedValC_In);
  and aCD (aCD_out, not_1_out, Byte_0_iCode[1], Byte_0_iCode[0], NeedValC_In);
  or or_1 (or_1_out, Abcd_out, aBc_out, aCD_out);
  Register #(.width(4)) rA_Reg (.D(Byte_1_rA_rB[3:0]), .en(NeedReg_In), .clk(Clk), .Q(rA));  // open: clr
  Register #(.width(4)) rB_Reg (.D(Byte_1_rA_rB[7:4]), .en(NeedReg_In), .clk(Clk), .Q(rB));  // open: clr
  Register Byte_2 (.D(Byte_2_Inp), .en(or_1_out), .clk(Clk), .Q(Byte_2_q[7:0]));  // open: clr
  Register Byte_3 (.D(Byte_3_Inp), .en(or_1_out), .clk(Clk), .Q(Byte_2_q[15:8]));  // open: clr
  Register Byte_4 (.D(Byte_4_Inp), .en(or_1_out), .clk(Clk), .Q(Byte_2_q[23:16]));  // open: clr
  Register Byte_5 (.D(Byte_5_Inp), .en(or_1_out), .clk(Clk), .Q(Byte_2_q[31:24]));  // open: clr
  Register Byte_6 (.D(Byte_6_Inp), .en(or_1_out), .clk(Clk), .Q(Byte_2_q[39:32]));  // open: clr
  Register Byte_7 (.D(Byte_7_Inp), .en(or_1_out), .clk(Clk), .Q(Byte_2_q[47:40]));  // open: clr
  Register Byte_8 (.D(Byte_8_Inp), .en(or_1_out), .clk(Clk), .Q(Byte_2_q[55:48]));  // open: clr
  Register Byte_9 (.D(Byte_9_Inp), .en(or_1_out), .clk(Clk), .Q(Byte_2_q[63:56]));  // open: clr
  Register #(.width(64)) register_1 (.D(Byte_2_q), .en(NeedValC_In), .clk(Clk), .Q(ValC));  // open: clr

  // Notes on the sheet:
  //   Pass in rA and rB val by reading iCode and read from Byte 1 or %rsp
  //   Get ValC data by reading iCode and iFun, determine its required memeory data size
  //   Reset Register somehow
endmodule

module ValP_logic (
  input  [63:0] PC_In,
  input  [3:0] iCode_Inp,
  input  CLK,
  output [63:0] ValP_Out
);

  wire [7:0] multiplexer_1_out;
  wire [63:0] adder_1_out;

  Multiplexer #(.select(4), .width(8)) multiplexer_1 (
    .in0({8{1'b0}}), .in1(8'h1), .in2(8'h2), .in3(8'ha), .in4(8'ha), .in5(8'ha), .in6(8'h2), .in7(8'h9),
    .in8(8'h9), .in9(8'h9), .in10(8'h2), .in11(8'h2), .in12(8'h2), .in13(8'h2), .in14(8'h2), .in15(8'h2),
    .out(multiplexer_1_out), .sel(iCode_Inp));
  Adder #(.width(64)) adder_1 (.a(PC_In), .b({{56{1'b0}}, multiplexer_1_out}), .out(adder_1_out));  // open: cin, cout
  Register #(.width(64)) register_1 (.D(adder_1_out), .clk(CLK), .Q(ValP_Out));  // open: en, clr
endmodule

module Align (
  input  NeedReg_In,
  input  [7:0] Byte_1_rA_rB,
  input  [7:0] Byte_2_Inp,
  input  [7:0] Byte_3_Inp,
  input  [7:0] Byte_4_Inp,
  input  [7:0] Byte_5_Inp,
  input  [7:0] Byte_6_Inp,
  input  [7:0] Byte_7_Inp,
  input  [7:0] Byte_8_Inp,
  input  [7:0] Byte_9_Inp,
  input  Clk,
  output [3:0] rA,
  output [3:0] rB,
  output [63:0] ValC
);

  wire [63:0] multiplexer_1_out;

  Multiplexer #(.width(64)) multiplexer_1 (
    .in0({Byte_8_Inp, Byte_7_Inp, Byte_6_Inp, Byte_5_Inp, Byte_4_Inp, Byte_3_Inp, Byte_2_Inp, Byte_1_rA_rB}),
    .in1({Byte_9_Inp, Byte_8_Inp, Byte_7_Inp, Byte_6_Inp, Byte_5_Inp, Byte_4_Inp, Byte_3_Inp, Byte_2_Inp}),
    .out(multiplexer_1_out), .sel(NeedReg_In));
  Register #(.width(4)) rA_Reg (.D(Byte_1_rA_rB[7:4]), .en(NeedReg_In), .clk(Clk), .Q(rA));  // open: clr
  Register #(.width(4)) rB_Reg (.D(Byte_1_rA_rB[3:0]), .en(NeedReg_In), .clk(Clk), .Q(rB));  // open: clr
  Register #(.width(64)) register_1 (.D(multiplexer_1_out), .clk(Clk), .Q(ValC));  // open: en, clr
endmodule

module SplitAndAlign (
  input  Enable,
  input  [7:0] Byte0,
  input  [7:0] Byte1,
  input  [7:0] Byte2,
  input  [7:0] Byte3,
  input  [7:0] Byte4,
  input  [7:0] Byte5,
  input  [7:0] Byte6,
  input  [7:0] Byte7,
  input  [7:0] Byte8,
  input  [7:0] Byte9,
  input  [63:0] CurrPC_In,
  input  CLK,
  output iCode_Error,
  output [3:0] iCode,
  output [3:0] iFun,
  output [3:0] rA,
  output [3:0] rB,
  output [63:0] ValC,
  output [63:0] valP
);

  wire reg_enable_1_t_reg;

  Split split_1 (.Byte_0_INP(Byte0), .Enable(Enable), .Clk(CLK), .INP_Error(iCode_Error), .iCode(iCode), .iFun(iFun));
  Reg_Enable reg_enable_1 (.iCode_inp(iCode), .T_Reg(reg_enable_1_t_reg));
  Align align_1 (
    .NeedReg_In(reg_enable_1_t_reg), .Byte_1_rA_rB(Byte1), .Byte_2_Inp(Byte2), .Byte_3_Inp(Byte3),
    .Byte_4_Inp(Byte4), .Byte_5_Inp(Byte5), .Byte_6_Inp(Byte6), .Byte_7_Inp(Byte7), .Byte_8_Inp(Byte8),
    .Byte_9_Inp(Byte9), .Clk(CLK), .rA(rA), .rB(rB), .ValC(ValC));
  ValP_logic valp_logic_1 (.PC_In(CurrPC_In), .iCode_Inp(iCode), .CLK(CLK), .ValP_Out(valP));

  // Notes on the sheet:
  //   Enable - taking one input at a time, could be replaced by clock implementation
endmodule

module Register_File (
  input  [63:0] valM,
  input  [63:0] valE,
  input  [3:0] dstE,
  input  [3:0] dstM,
  input  W_E,
  input  W_M,
  input  [3:0] srcA,
  input  [3:0] srcB,
  input  WB_CLK,
  output [63:0] valA,
  output [63:0] valB
);

  wire demultiplexer_1_out0, demultiplexer_1_out1, demultiplexer_1_out2, demultiplexer_1_out3,
       demultiplexer_1_out4, demultiplexer_1_out5, demultiplexer_1_out6, demultiplexer_1_out7,
       demultiplexer_1_out8, demultiplexer_1_out9, demultiplexer_1_out10, demultiplexer_1_out11,
       demultiplexer_1_out12, demultiplexer_1_out13, demultiplexer_1_out14, demultiplexer_1_out15, not_1_out,
       or_1_out;
  wire [3:0] multiplexer_2_out;
  wire [63:0] multiplexer_1_out, r8_q, r9_q, r10_q, r11_q, r12_q, r13_q, r14_q, r15_q, rax_q, rbp_q, rbx_q,
       rcx_q, rdi_q, rdx_q, rsi_q, rsp_q;

  or or_1 (or_1_out, W_E, W_M);
  Multiplexer #(.width(64)) multiplexer_1 (.in0(valM), .in1(valE), .out(multiplexer_1_out), .sel(W_E));
  Demultiplexer #(.select(4)) demultiplexer_1 (
    .out0(demultiplexer_1_out0), .out1(demultiplexer_1_out1), .out2(demultiplexer_1_out2),
    .out3(demultiplexer_1_out3), .out4(demultiplexer_1_out4), .out5(demultiplexer_1_out5),
    .out6(demultiplexer_1_out6), .out7(demultiplexer_1_out7), .out8(demultiplexer_1_out8),
    .out9(demultiplexer_1_out9), .out10(demultiplexer_1_out10), .out11(demultiplexer_1_out11),
    .out12(demultiplexer_1_out12), .out13(demultiplexer_1_out13), .out14(demultiplexer_1_out14),
    .out15(demultiplexer_1_out15), .in(or_1_out), .sel(multiplexer_2_out));
  Multiplexer #(.width(4)) multiplexer_2 (.in0(dstE), .in1(dstM), .out(multiplexer_2_out), .sel(not_1_out));
  not not_1 (not_1_out, W_E);
  Register #(.width(64)) rax (.D(multiplexer_1_out), .en(demultiplexer_1_out0), .clk(WB_CLK), .Q(rax_q));  // open: clr
  Register #(.width(64)) rsp (.D(multiplexer_1_out), .en(demultiplexer_1_out4), .clk(WB_CLK), .Q(rsp_q));  // open: clr
  Register #(.width(64)) r8 (.D(multiplexer_1_out), .en(demultiplexer_1_out8), .clk(WB_CLK), .Q(r8_q));  // open: clr
  Register #(.width(64)) r12 (.D(multiplexer_1_out), .en(demultiplexer_1_out12), .clk(WB_CLK), .Q(r12_q));  // open: clr
  Register #(.width(64)) rcx (.D(multiplexer_1_out), .en(demultiplexer_1_out1), .clk(WB_CLK), .Q(rcx_q));  // open: clr
  Register #(.width(64)) rbp (.D(multiplexer_1_out), .en(demultiplexer_1_out5), .clk(WB_CLK), .Q(rbp_q));  // open: clr
  Register #(.width(64)) r9 (.D(multiplexer_1_out), .en(demultiplexer_1_out9), .clk(WB_CLK), .Q(r9_q));  // open: clr
  Register #(.width(64)) r13 (.D(multiplexer_1_out), .en(demultiplexer_1_out13), .clk(WB_CLK), .Q(r13_q));  // open: clr
  Register #(.width(64)) rdx (.D(multiplexer_1_out), .en(demultiplexer_1_out2), .clk(WB_CLK), .Q(rdx_q));  // open: clr
  Register #(.width(64)) rsi (.D(multiplexer_1_out), .en(demultiplexer_1_out6), .clk(WB_CLK), .Q(rsi_q));  // open: clr
  Register #(.width(64)) r10 (.D(multiplexer_1_out), .en(demultiplexer_1_out10), .clk(WB_CLK), .Q(r10_q));  // open: clr
  Register #(.width(64)) r14 (.D(multiplexer_1_out), .en(demultiplexer_1_out14), .clk(WB_CLK), .Q(r14_q));  // open: clr
  Register #(.width(64)) rbx (.D(multiplexer_1_out), .en(demultiplexer_1_out3), .clk(WB_CLK), .Q(rbx_q));  // open: clr
  Register #(.width(64)) rdi (.D(multiplexer_1_out), .en(demultiplexer_1_out7), .clk(WB_CLK), .Q(rdi_q));  // open: clr
  Register #(.width(64)) r11 (.D(multiplexer_1_out), .en(demultiplexer_1_out11), .clk(WB_CLK), .Q(r11_q));  // open: clr
  Register #(.width(64)) r15 (.D(multiplexer_1_out), .en(demultiplexer_1_out15), .clk(WB_CLK), .Q(r15_q));  // open: clr
  Multiplexer #(.select(4), .width(64)) multiplexer_3 (
    .in0(rax_q), .in1(rcx_q), .in2(rdx_q), .in3(rbx_q), .in4(rsp_q), .in5(rbp_q), .in6(rsi_q), .in7(rdi_q),
    .in8(r8_q), .in9(r9_q), .in10(r10_q), .in11(r11_q), .in12(r12_q), .in13(r13_q), .in14(r14_q),
    .in15(r15_q), .out(valA), .sel(srcA));
  Multiplexer #(.select(4), .width(64)) multiplexer_4 (
    .in0(rax_q), .in1(rcx_q), .in2(rdx_q), .in3(rbx_q), .in4(rsp_q), .in5(rbp_q), .in6(rsi_q), .in7(rdi_q),
    .in8(r8_q), .in9(r9_q), .in10(r10_q), .in11(r11_q), .in12(r12_q), .in13(r13_q), .in14(r14_q),
    .in15(r15_q), .out(valB), .sel(srcB));
endmodule

module WB_CLK_Logic (
  input  [3:0] Icode,
  input  clk,
  output W_E,
  output W_M
);

  wire eight_out, eleven2_out, eleven_out, five_out, nine_out, not_1_out, not_2_out, or_1_out, or_2_out,
       register_1_q, six_out, ten_out, three_out, two_out;

  and two (two_out, ~Icode[0], Icode[1], ~Icode[2], ~Icode[3]);  // AND_Gate
  and three (three_out, Icode[0], Icode[1], ~Icode[2], ~Icode[3]);  // AND_Gate
  and five (five_out, Icode[0], ~Icode[1], Icode[2], ~Icode[3]);  // AND_Gate
  and six (six_out, ~Icode[0], Icode[1], Icode[2], ~Icode[3]);  // AND_Gate
  and eight (eight_out, ~Icode[0], ~Icode[1], ~Icode[2], Icode[3]);  // AND_Gate
  and ten (ten_out, ~Icode[0], Icode[1], ~Icode[2], Icode[3]);  // AND_Gate
  and nine (nine_out, Icode[0], ~Icode[1], ~Icode[2], Icode[3]);  // AND_Gate
  and eleven (eleven_out, Icode[0], Icode[1], ~Icode[2], Icode[3]);  // AND_Gate
  and eleven2 (eleven2_out, Icode[0], Icode[1], ~Icode[2], Icode[3]);  // AND_Gate
  or or_1 (or_1_out, two_out, three_out, six_out, eight_out, nine_out, ten_out, eleven_out);
  or or_2 (or_2_out, five_out, eleven2_out);
  Register #(.width(1)) register_1 (.D(not_1_out), .clk(clk), .Q(register_1_q));  // open: en, clr
  not not_1 (not_1_out, register_1_q);
  not not_2 (not_2_out, register_1_q);
  Multiplexer multiplexer_1 (.in0(1'b0), .in1(not_2_out), .out(W_E), .sel(or_1_out));
  Multiplexer multiplexer_2 (.in0(1'b0), .in1(register_1_q), .out(W_M), .sel(or_2_out));
endmodule

module WB_DEST_logic (
  input  [3:0] Icode,
  input  [3:0] iRB,
  output [3:0] DestE
);

  wire RB_out, six_out, three_out, two_out;

  and two (two_out, ~Icode[0], Icode[1], ~Icode[2], ~Icode[3]);  // AND_Gate
  and three (three_out, Icode[0], Icode[1], ~Icode[2], ~Icode[3]);  // AND_Gate
  and six (six_out, ~Icode[0], Icode[1], Icode[2], ~Icode[3]);  // AND_Gate
  or RB (RB_out, two_out, three_out, six_out);
  Multiplexer #(.width(4)) multiplexer_1 (.in0(4'b0100), .in1(iRB), .out(DestE), .sel(RB_out));
endmodule

module PC_Update (
  input  [63:0] valP,
  input  JMP,
  input  [63:0] valC,
  input  [63:0] valM,
  input  [3:0] icode,
  output [63:0] newPC
);

  wire [63:0] multiplexer_1_out;

  Multiplexer #(.width(64)) multiplexer_1 (.in0(valP), .in1(valC), .out(multiplexer_1_out), .sel(JMP));
  Multiplexer #(.select(4), .width(64)) multiplexer_2 (
    .in0(valP), .in1(valP), .in2(valP), .in3(valP), .in4(valP), .in5(valP), .in6(valP),
    .in7(multiplexer_1_out), .in8(valC), .in9(valM), .in10(valP), .in11(valP), .in12(valP), .in13(valP),
    .in14(valP), .in15(valP), .out(newPC), .sel(icode));
endmodule

module Execute (
  input  [63:0] ValA,
  input  [63:0] ValB,
  input  [3:0] iCode,
  input  [3:0] iFun,
  input  [63:0] ValC,
  input  clk,
  output [63:0] ValE_Out,
  output cond_out
);

  wire setcc_1_setcc_out;
  wire [1:0] alu_1_previouscc, alu_fun_1_alu_fun_out, cc_1_cc_out;
  wire [63:0] alu_a_1_alu_a_out, alu_b_1_alu_b_out;

  ALU_fun alu_fun_1 (.icode_Inp(iCode), .ifun_Inp(iFun), .ALU_fun_Out(alu_fun_1_alu_fun_out));
  ALU_A alu_a_1 (.icode_Inp(iCode), .ValC(ValC), .ValA(ValA), .ALU_A_Out(alu_a_1_alu_a_out));
  ALU_B alu_b_1 (.icode_Inp(iCode), .ValB(ValB), .ALU_B_Out(alu_b_1_alu_b_out));
  setCC setcc_1 (.icode_Inp(iCode), .setCC_Out(setcc_1_setcc_out));
  ALU alu_1 (
    .ALU_fun_Inp(alu_fun_1_alu_fun_out), .ALU_A(alu_a_1_alu_a_out), .ALU_B(alu_b_1_alu_b_out),
    .ValE(ValE_Out), .previousCC(alu_1_previouscc));
  CC cc_1 (.previousCC(alu_1_previouscc), .setCC_EN(setcc_1_setcc_out), .clk(clk), .CC_Out(cc_1_cc_out));
  Cond cond_1 (.iFun(iFun), .CC_Inp(cc_1_cc_out), .cond_Out(cond_out));
endmodule

module ALU (
  input  [1:0] ALU_fun_Inp,
  input  [63:0] ALU_A,
  input  [63:0] ALU_B,
  output [63:0] ValE,
  output [1:0] previousCC
);

  wire [63:0] adder_1_out, and_1_out, subtractor_1_out, xor_1_out;

  Adder #(.width(64)) adder_1 (.a(ALU_A), .b(ALU_B), .out(adder_1_out));  // open: cin, cout
  Subtractor #(.width(64)) subtractor_1 (.a(ALU_B), .b(ALU_A), .out(subtractor_1_out));  // open: bin, bout
  assign and_1_out = ALU_A & ALU_B;  // AND_Gate and_1, 64 bits wide
  assign xor_1_out = ALU_A ^ ALU_B;  // XOR_Gate xor_1, 64 bits wide
  Multiplexer #(.select(2), .width(64)) multiplexer_1 (
    .in0(adder_1_out), .in1(subtractor_1_out), .in2(and_1_out), .in3(xor_1_out), .out(ValE), .sel(ALU_fun_Inp));
  Comparator #(.width(64)) comparator_1 (.a(ValE), .b({64{1'b0}}), .eq(previousCC[0]), .lt(previousCC[1]));  // open: gt

  // Notes on the sheet:
  //   ALU Computation
  //   Setting Previous CC
  //   01 = ZeroF
  //   10 = SignedF
endmodule

module ALU_fun (
  input  [3:0] icode_Inp,
  input  [3:0] ifun_Inp,
  output [1:0] ALU_fun_Out
);

  wire aBCd_out, Abd_out, not_1_out, not_3_out, not_4_out, not_5_out;
  wire [1:0] multiplexer_1_out;

  not not_1 (not_1_out, icode_Inp[0]);
  // NOT_Gate not_2 has open pins: in=icode_Inp[1], out=open
  not not_3 (not_3_out, icode_Inp[2]);
  not not_4 (not_4_out, icode_Inp[3]);
  and Abd (Abd_out, not_1_out, not_3_out, icode_Inp[3]);
  and aBCd (aBCd_out, not_4_out, icode_Inp[2], icode_Inp[1], not_1_out);
  Multiplexer #(.width(2)) multiplexer_1 (.in0(2'b00), .in1(2'b01), .out(multiplexer_1_out), .sel(Abd_out));
  not not_5 (not_5_out, aBCd_out);
  assign ALU_fun_Out = not_5_out ? multiplexer_1_out : 2'bz;  // Controlled_Buffer controlled_buffer_1
  assign ALU_fun_Out = aBCd_out ? ifun_Inp[1:0] : 2'bz;  // Controlled_Buffer controlled_buffer_2

  // Notes on the sheet:
  //   0 = add
  //   2 = and
  //   1 = sub
  //   3 = xor
endmodule

module ALU_A (
  input  [3:0] icode_Inp,
  input  [63:0] ValC,
  input  [63:0] ValA,
  output [63:0] ALU_A_Out
);

  wire [1:0] alu_a_selector_1_select_out;

  ALU_A_Selector alu_a_selector_1 (.icode_Inp(icode_Inp), .Select_Out(alu_a_selector_1_select_out));
  Multiplexer #(.select(2), .width(64)) multiplexer_1 (
    .in0(ValC), .in1(ValA), .in2(64'h8), .in3({64{1'b0}}), .out(ALU_A_Out), .sel(alu_a_selector_1_select_out));

  // Notes on the sheet:
  //   0 = valC
  //   1 = valA
  //   2 = 8
  //   3 = 0 (default)
endmodule

module ALU_A_Selector (
  input  [3:0] icode_Inp,
  output [1:0] Select_Out
);

  wire Ab_out, abc_out, aBCD_out, aCd_out, and_1_out, not_1_out, not_2_out, not_3_out, not_4_out, or_1_out,
       xnor_1_out;

  not not_1 (not_1_out, icode_Inp[0]);
  not not_2 (not_2_out, icode_Inp[1]);
  not not_3 (not_3_out, icode_Inp[2]);
  not not_4 (not_4_out, icode_Inp[3]);
  and aCd (aCd_out, not_1_out, icode_Inp[1], not_4_out);
  and Ab (Ab_out, icode_Inp[3], not_3_out);
  and aBCD (aBCD_out, not_4_out, icode_Inp[2], icode_Inp[1], icode_Inp[0]);
  and abc (abc_out, not_4_out, not_3_out, not_2_out);
  xnor xnor_1 (xnor_1_out, aCd_out, Ab_out);
  or or_1 (or_1_out, aBCD_out, abc_out);
  and and_1 (and_1_out, xnor_1_out, or_1_out);
  Multiplexer multiplexer_1 (.in0(aCd_out), .in1(1'b1), .out(Select_Out[0]), .sel(and_1_out));
  Multiplexer multiplexer_2 (.in0(Ab_out), .in1(1'b1), .out(Select_Out[1]), .sel(and_1_out));

  // Notes on the sheet:
  //   0 = valC
  //   1 = valA
  //   2 = 8
  //   3 = 0 (default)
endmodule

module ALU_B (
  input  [3:0] icode_Inp,
  input  [63:0] ValB,
  output [63:0] ALU_B_Out
);

  wire alu_b_selector_1_select_out;

  ALU_B_Selector alu_b_selector_1 (.icode_Inp(icode_Inp), .Select_Out(alu_b_selector_1_select_out));
  Multiplexer #(.width(64)) multiplexer_1 (
    .in0({64{1'b0}}), .in1(ValB), .out(ALU_B_Out), .sel(alu_b_selector_1_select_out));
endmodule

module ALU_B_Selector (
  input  [3:0] icode_Inp,
  output Select_Out
);

  wire Ab_out, aBc_out, aBd_out, not_1_out, not_2_out, not_3_out, not_4_out;

  not not_1 (not_1_out, icode_Inp[0]);
  not not_2 (not_2_out, icode_Inp[1]);
  not not_3 (not_3_out, icode_Inp[2]);
  not not_4 (not_4_out, icode_Inp[3]);
  and aBc (aBc_out, not_2_out, icode_Inp[2], not_4_out);
  and aBd (aBd_out, not_1_out, icode_Inp[2], not_4_out);
  and Ab (Ab_out, not_3_out, icode_Inp[3]);
  or or_1 (Select_Out, aBc_out, aBd_out, Ab_out);
endmodule

module setCC (
  input  [3:0] icode_Inp,
  output setCC_Out
);

  wire not_1_out, not_4_out;

  not not_1 (not_1_out, icode_Inp[0]);
  // NOT_Gate not_2 has open pins: in=icode_Inp[1], out=open
  // NOT_Gate not_3 has open pins: in=icode_Inp[2], out=open
  not not_4 (not_4_out, icode_Inp[3]);
  and aBC (setCC_Out, not_1_out, not_4_out, icode_Inp[1], icode_Inp[2]);
endmodule

module CC (
  input  [1:0] previousCC,
  input  setCC_EN,
  input  clk,
  output [1:0] CC_Out
);

  Register #(.width(2)) register_1 (.D(previousCC), .en(setCC_EN), .clk(clk), .Q(CC_Out));  // open: clr
endmodule

module Cond (
  input  [3:0] iFun,
  input  [1:0] CC_Inp,
  output cond_Out
);

  wire and_1_out, and_2_out, and_3_out, je_out, jg_out, jge_out, jl_out, jle_out, jmp_out, jne_out,
       not_1_out, not_2_out, not_3_out, not_4_out, not_5_out, not_6_out, or_1_out;

  not not_1 (not_1_out, iFun[0]);
  not not_2 (not_2_out, iFun[1]);
  not not_3 (not_3_out, iFun[2]);
  not not_4 (not_4_out, iFun[3]);
  not not_5 (not_5_out, CC_Inp[0]);
  not not_6 (not_6_out, CC_Inp[1]);
  and and_1 (and_1_out, iFun[0], not_2_out, not_3_out, not_4_out);
  and and_2 (and_2_out, CC_Inp[0], not_6_out);
  and and_3 (and_3_out, not_5_out, CC_Inp[1]);
  or or_1 (or_1_out, and_2_out, and_3_out);
  and jmp (jmp_out, not_4_out, not_3_out, not_2_out, not_1_out);
  and jle (jle_out, and_1_out, or_1_out);
  and jl (jl_out, not_1_out, iFun[1], not_3_out, not_4_out, CC_Inp[1]);
  and je (je_out, iFun[0], iFun[1], not_3_out, not_4_out, CC_Inp[0]);
  and jne (jne_out, not_1_out, not_2_out, iFun[2], not_4_out, not_5_out);
  and jge (jge_out, not_2_out, not_4_out, iFun[2], iFun[0], not_6_out);
  and jg (jg_out, not_1_out, iFun[2], iFun[1], not_4_out, not_6_out, not_5_out);
  or or_2 (cond_Out, jmp_out, jle_out, jl_out, je_out, jne_out, jge_out, jg_out);

  // Notes on the sheet:
  //   001 = ZeroF
  //   010 = SignedF
  //   100 = OverflowF
endmodule

module Memory_main (
  input  [63:0] Val_E,
  input  [63:0] Val_P,
  input  [3:0] icode,
  input  [63:0] Val_A,
  input  CLK,
  output [63:0] ValM
);

  wire memory_read_1_m_read, memory_write_1_m_write;
  wire [11:0] memory_address_1_address_in;
  wire [63:0] memory_data_1_data_in;

  Memory_Address memory_address_1 (
    .Val_E(Val_E[11:0]), .Val_A(Val_A[11:0]), .icode(icode), .Address_in(memory_address_1_address_in));
  Memory_Write memory_write_1 (.icode(icode), .M_Write(memory_write_1_m_write));
  Memory_Read memory_read_1 (.icode(icode), .M_Read(memory_read_1_m_read));
  Memory_Data memory_data_1 (.Val_P(Val_P), .Val_A(Val_A), .icode(icode), .Data_in(memory_data_1_data_in));
  Data_Memory data_memory_1 (
    .Address(memory_address_1_address_in), .Write(memory_write_1_m_write), .Read(memory_read_1_m_read),
    .Data(memory_data_1_data_in), .CLK(CLK), .Val_M(ValM));
endmodule

module Memory_Read (
  input  [3:0] icode,
  output M_Read
);

  wire mrmovq_out, not_1_out, not_2_out, not_3_out, pop_out, ret_out;

  not not_1 (not_1_out, icode[3]);
  not not_2 (not_2_out, icode[2]);
  not not_3 (not_3_out, icode[1]);
  and pop (pop_out, icode[3], not_2_out, icode[1], icode[0]);
  and ret (ret_out, icode[3], not_2_out, not_3_out, icode[0]);
  and mrmovq (mrmovq_out, not_1_out, icode[2], not_3_out, icode[0]);
  or or_1 (M_Read, pop_out, ret_out, mrmovq_out);
endmodule

module Memory_Write (
  input  [3:0] icode,
  output M_Write
);

  wire call_out, not_1_out, not_2_out, not_3_out, not_4_out, push_out, rmmovq_out;

  not not_1 (not_1_out, icode[3]);
  not not_2 (not_2_out, icode[2]);
  not not_3 (not_3_out, icode[1]);
  not not_4 (not_4_out, icode[0]);
  and push (push_out, icode[3], not_2_out, icode[1], not_4_out);
  and call (call_out, icode[3], not_2_out, not_3_out, not_4_out);
  and rmmovq (rmmovq_out, not_1_out, icode[2], not_3_out, not_4_out);
  or or_1 (M_Write, push_out, call_out, rmmovq_out);
endmodule

module Data_Memory (
  input  [11:0] Address,
  input  Write,
  input  Read,
  input  [63:0] Data,
  input  CLK,
  output [63:0] Val_M
);

  wire and_1_out, decoder_1_out0, decoder_1_out1, decoder_1_out2, decoder_1_out3, decoder_1_out4,
       decoder_1_out5, decoder_1_out6, decoder_1_out7;
  wire [2:0] counter_1_q;
  wire [7:0] multiplexer_1_out, portio_1_p3, ram_1_dout;
  wire [11:0] adder_1_out;
  wire [11:3] counter_1_q_2;

  Counter #(.max('h7), .width(12)) counter_1 (
    .up(1'b1), .count(1'b1), .clk(CLK), .D(Address), .Q({counter_1_q_2, counter_1_q}));  // open: clr, load, carry
  Adder #(.width(12)) adder_1 (.a(Address), .b({counter_1_q_2, counter_1_q}), .out(adder_1_out));  // open: cin, cout
  Multiplexer #(.select(3), .width(8)) multiplexer_1 (
    .in0(Data[7:0]), .in1(Data[15:8]), .in2(Data[23:16]), .in3(Data[31:24]), .in4(Data[39:32]),
    .in5(Data[47:40]), .in6(Data[55:48]), .in7(Data[63:56]), .out(multiplexer_1_out), .sel(counter_1_q));
  RAM #(.addrWidth(12)) ram_1 (
    .addr(adder_1_out), .we(Write), .oe(Read), .clk(CLK), .din(multiplexer_1_out), .dout(ram_1_dout));
  // PortIO portio_1: pin names not known; wires that end beside it: Read, ram_1_dout, portio_1_p3
  and and_1 (and_1_out, CLK, Read);
  Decoder #(.select(3)) decoder_1 (
    .out0(decoder_1_out0), .out1(decoder_1_out1), .out2(decoder_1_out2), .out3(decoder_1_out3),
    .out4(decoder_1_out4), .out5(decoder_1_out5), .out6(decoder_1_out6), .out7(decoder_1_out7),
    .sel(counter_1_q));  // open: en
  Register #(.trigger("high")) register_1 (
    .D(portio_1_p3), .en(decoder_1_out1), .Q(Val_M[7:0]), .clk(and_1_out));  // open: clr
  Register #(.trigger("high")) register_2 (
    .D(portio_1_p3), .en(decoder_1_out2), .Q(Val_M[15:8]), .clk(and_1_out));  // open: clr
  Register #(.trigger("high")) register_3 (
    .D(portio_1_p3), .en(decoder_1_out3), .Q(Val_M[23:16]), .clk(and_1_out));  // open: clr
  Register #(.trigger("high")) register_4 (
    .D(portio_1_p3), .en(decoder_1_out4), .Q(Val_M[31:24]), .clk(and_1_out));  // open: clr
  Register #(.trigger("high")) register_5 (
    .D(portio_1_p3), .en(decoder_1_out5), .Q(Val_M[39:32]), .clk(and_1_out));  // open: clr
  Register #(.trigger("high")) register_6 (
    .D(portio_1_p3), .en(decoder_1_out6), .Q(Val_M[47:40]), .clk(and_1_out));  // open: clr
  Register #(.trigger("high")) register_7 (
    .D(portio_1_p3), .en(decoder_1_out7), .Q(Val_M[55:48]), .clk(and_1_out));  // open: clr
  Register #(.trigger("high")) register_8 (
    .D(portio_1_p3), .en(decoder_1_out0), .Q(Val_M[63:56]), .clk(and_1_out));  // open: clr
endmodule

module Memory_Address (
  input  [11:0] Val_E,
  input  [11:0] Val_A,
  input  [3:0] icode,
  output [11:0] Address_in
);

  wire not_1_out, not_2_out, or_1_out, pop_out, ret_out;

  not not_1 (not_1_out, icode[2]);
  not not_2 (not_2_out, icode[1]);
  and pop (pop_out, icode[3], not_1_out, icode[1], icode[0]);
  and ret (ret_out, icode[3], not_1_out, not_2_out, icode[0]);
  Multiplexer #(.width(12)) multiplexer_1 (.in0(Val_E), .in1(Val_A), .out(Address_in), .sel(or_1_out));
  or or_1 (or_1_out, pop_out, ret_out);
endmodule

module Memory_Data (
  input  [63:0] Val_P,
  input  [63:0] Val_A,
  input  [3:0] icode,
  output [63:0] Data_in
);

  wire not_1_out, not_2_out, not_3_out, not_4_out, or_1_out, push_out, rmmovq_out;

  not not_1 (not_1_out, icode[3]);
  not not_2 (not_2_out, icode[2]);
  not not_3 (not_3_out, icode[1]);
  not not_4 (not_4_out, icode[0]);
  and push (push_out, icode[3], not_2_out, icode[1], not_4_out);
  and rmmovq (rmmovq_out, not_1_out, icode[2], not_3_out, not_4_out);
  Multiplexer #(.width(64)) multiplexer_1 (.in0(Val_P), .in1(Val_A), .out(Data_in), .sel(or_1_out));
  or or_1 (or_1_out, push_out, rmmovq_out);
endmodule

module srcA (
  input  [3:0] icode,
  input  [3:0] rA,
  output [3:0] src
);

  wire and_1_out, and_2_out, eigth_out, RB_out;

  and eigth (eigth_out, ~icode[0], ~icode[1], ~icode[2], icode[3]);  // AND_Gate
  and and_1 (and_1_out, icode[0], ~icode[1], ~icode[2], icode[3]);  // AND_Gate
  and and_2 (and_2_out, icode[0], icode[1], ~icode[2], icode[3]);  // AND_Gate
  or RB (RB_out, eigth_out, and_1_out, and_2_out);
  Multiplexer #(.width(4)) multiplexer_1 (.in0(rA), .in1(4'b0100), .out(src), .sel(RB_out));

  // Notes on the sheet:
  //   srcA
endmodule

module srcB (
  input  [3:0] icode,
  input  [3:0] rB,
  output [3:0] src
);

  wire and_1_out, and_2_out, and_3_out, eigth_out, or_1_out;

  and eigth (eigth_out, ~icode[0], ~icode[1], ~icode[2], icode[3]);  // AND_Gate
  and and_1 (and_1_out, icode[0], ~icode[1], ~icode[2], icode[3]);  // AND_Gate
  and and_2 (and_2_out, icode[0], icode[1], ~icode[2], icode[3]);  // AND_Gate
  and and_3 (and_3_out, ~icode[0], icode[1], ~icode[2], icode[3]);  // AND_Gate
  or or_1 (or_1_out, eigth_out, and_1_out, and_2_out, and_3_out);
  Multiplexer #(.width(4)) multiplexer_1 (.in0(rB), .in1(4'b0100), .out(src), .sel(or_1_out));

  // Notes on the sheet:
  //   srcB
endmodule
